// Logisim project Guia04.circ as structural Verilog
module Numero1 (
  input  z,
  input  x,
  input  y,
  input  z_2,
  input  x_2,
  input  y_2,
  input  z_3,
  input  x_3,
  input  y_3,
  output S,
  output S_2,
  output S_3
);

  wire and_1_out, and_2_out, not_1_out, not_2_out, not_3_out, not_4_out, not_5_out, not_6_out, not_7_out,
       not_8_out, or_1_out;

  not not_1 (not_1_out, y);
  not not_2 (not_2_out, x_2);
  not not_3 (not_3_out, x_3);
  not not_4 (not_4_out, y_3);
  or or_1 (or_1_out, x, not_1_out);
  and and_1 (and_1_out, not_2_out, y_2);
  and and_2 (and_2_out, not_3_out, not_4_out);
  not not_5 (not_5_out, or_1_out);
  not not_6 (not_6_out, z_2);
  not not_7 (not_7_out, and_1_out);
  not not_8 (not_8_out, and_2_out);
  and and_3 (S, z, not_5_out);
  and and_4 (S_2, not_6_out, not_7_out);
  and and_5 (S_3, z_3, not_8_out);

  // Notes on the sheet:
  //   Numero 1
  //   b)
  //   c)
  //   d)
endmodule

module Numero2 (
  input  x,
  input  y,
  input  d,
  input  in_4,
  input  e,
  input  in_6,
  output out_7,
  output out_8,
  output out_9
);

  wire not_1_out;

  and and_1 (out_7, x, y);
  or or_1 (out_8, d, in_4);
  not not_1 (not_1_out, in_6);
  or or_2 (out_9, e, not_1_out);

  // Notes on the sheet:
  //   Numero 2
  //   a)
endmodule

module Numero3 (
  input  z,
  input  y,
  input  x,
  input  z_2,
  input  w,
  input  y_2,
  input  x_2,
  output out_8,
  output out_9
);

  wire and_2_out, and_3_out;

  and and_1 (out_8, z, y, x);
  and and_2 (and_2_out, z_2, w);
  and and_3 (and_3_out, y_2, x_2);
  and and_4 (out_9, and_2_out, and_3_out);

  // Notes on the sheet:
  //   Numero 3
  //   b)
  //   d)
endmodule

module Numero4 (
  input  x,
  input  w,
  input  z,
  input  x_2,
  input  y,
  input  w_2,
  input  z_2,
  input  x_3,
  input  y_2,
  input  w_3,
  input  z_3,
  output out_12,
  output out_13,
  output out_14
);

  or or_1 (out_12, x, w, z);
  or or_2 (out_13, x_2, y, w_2, z_2);
  or or_3 (out_14, x_3, y_2, w_3, z_3);

  // Notes on the sheet:
  //   Numero 4
  //   a)
  //   c)
  //   e)
endmodule

module Numero5 (
  input  x,
  input  y,
  input  x_2,
  input  y_2,
  input  x_3,
  input  y_3,
  input  x_4,
  input  y_4,
  input  x_5,
  input  y_5,
  input  z,
  input  x_6,
  input  y_6,
  input  z_2,
  input  x_7,
  input  y_7,
  input  z_3,
  input  x_8,
  input  y_8,
  input  z_4,
  input  x_9,
  input  y_9,
  input  z_5,
  input  x_10,
  input  y_10,
  input  z_6,
  input  x_11,
  input  y_11,
  input  z_7,
  input  x_12,
  input  y_12,
  input  z_8,
  output S,
  output S_2,
  output out_35,
  output out_36
);

  wire and_1_out, and_2_out, and_3_out, and_4_out, and_5_out, and_6_out, and_7_out, and_8_out, not_1_out,
       not_2_out, not_3_out, not_4_out, not_5_out, not_6_out, not_7_out, not_8_out, not_9_out, not_10_out,
       not_11_out, not_12_out, not_13_out, not_14_out, or_1_out, or_2_out, or_3_out, or_4_out, or_6_out,
       or_7_out, or_8_out, or_9_out;

  not not_1 (not_1_out, x);
  or or_1 (or_1_out, x_3, y_3);
  not not_2 (not_2_out, x_4);
  not not_3 (not_3_out, x_5);
  not not_4 (not_4_out, y_5);
  not not_5 (not_5_out, z);
  not not_6 (not_6_out, x_6);
  not not_7 (not_7_out, y_6);
  not not_8 (not_8_out, x_7);
  not not_9 (not_9_out, y_8);
  not not_10 (not_10_out, z_4);
  not not_11 (not_11_out, z_5);
  not not_12 (not_12_out, y_11);
  not not_13 (not_13_out, x_12);
  not not_14 (not_14_out, z_8);
  and and_1 (and_1_out, not_1_out, y);
  and and_2 (and_2_out, x_2, y_2);
  or or_2 (or_2_out, not_2_out, y_4);
  and and_3 (and_3_out, not_3_out, not_4_out, not_5_out);
  and and_4 (and_4_out, not_6_out, not_7_out, z_2);
  and and_5 (and_5_out, not_8_out, y_7, z_3);
  and and_6 (and_6_out, x_8, not_9_out, not_10_out);
  and and_7 (and_7_out, x_9, y_9, not_11_out);
  and and_8 (and_8_out, x_10, y_10, z_6);
  or or_3 (or_3_out, x_11, not_12_out, z_7);
  or or_4 (or_4_out, not_13_out, y_12, not_14_out);
  or or_5 (S, and_1_out, and_2_out);
  buf and_9 (S_2, or_1_out);  // AND_Gate
  or or_6 (or_6_out, and_3_out, and_4_out);
  or or_7 (or_7_out, and_5_out, and_6_out);
  or or_8 (or_8_out, and_7_out, and_8_out);
  and and_10 (out_36, or_3_out, or_4_out);
  or or_9 (or_9_out, or_6_out, or_7_out);
  or or_10 (out_35, or_9_out, or_8_out);

  // Notes on the sheet:
  //   Numero 5
  //   a)
  //   c)
  //   SOP
  //   POS
  //   POS
  //   SOP
endmodule
