// Logisim project Guia_12.circ as structural Verilog
module Numero1 (
  input  ADDR,
  input  R_W,
  input  Input,
  input  Clear,
  output out_5,
  output out_6,
  output out_7,
  output out_8
);

  wire and_1_out, CLK_out, not_1_out, not_2_out, not_3_out, not_4_out;

  Clock CLK (.out(CLK_out));
  and and_1 (and_1_out, ADDR, R_W, CLK_out);
  not not_1 (not_1_out, Input);
  J_K_Flip_Flop j_k_ff_1 (.J(Input), .clk(and_1_out), .K(not_1_out), .Q(out_5), .reset(Clear));  // open: Qn, preset
  not not_2 (not_2_out, out_5);
  J_K_Flip_Flop j_k_ff_2 (.J(out_5), .clk(and_1_out), .K(not_2_out), .Q(out_6), .reset(Clear));  // open: Qn, preset
  not not_3 (not_3_out, out_6);
  J_K_Flip_Flop j_k_ff_3 (.J(out_6), .clk(and_1_out), .K(not_3_out), .Q(out_7), .reset(Clear));  // open: Qn, preset
  not not_4 (not_4_out, out_7);
  J_K_Flip_Flop j_k_ff_4 (.J(out_7), .clk(and_1_out), .K(not_4_out), .Q(out_8), .reset(Clear));  // open: Qn, preset
endmodule

module Numero2 (
  input  INPUT,
  input  in_2,
  input  in_3,
  input  in_4,
  input  in_5,
  input  in_6,
  input  in_7,
  input  in_8,
  input  ADDR,
  input  R_W,
  output out_11,
  output out_12,
  output out_13,
  output out_14,
  output out_15,
  output out_16,
  output out_17,
  output out_18
);

  wire and_1_out, CLK_out, not_1_out, not_2_out, not_3_out, not_4_out, not_5_out, not_6_out, not_7_out,
       not_8_out;

  Clock CLK (.out(CLK_out));
  and and_1 (and_1_out, ADDR, R_W, CLK_out);
  not not_1 (not_1_out, INPUT);
  J_K_Flip_Flop j_k_ff_1 (.J(INPUT), .clk(and_1_out), .K(not_1_out), .Q(out_11));  // open: Qn, preset, reset
  not not_2 (not_2_out, in_2);
  J_K_Flip_Flop j_k_ff_2 (.J(in_2), .clk(and_1_out), .K(not_2_out), .Q(out_12));  // open: Qn, preset, reset
  J_K_Flip_Flop j_k_ff_3 (.J(in_3), .clk(and_1_out), .K(not_3_out), .Q(out_13));  // open: Qn, preset, reset
  not not_3 (not_3_out, in_3);
  not not_4 (not_4_out, in_4);
  J_K_Flip_Flop j_k_ff_4 (.J(in_4), .clk(and_1_out), .K(not_4_out), .Q(out_14));  // open: Qn, preset, reset
  not not_5 (not_5_out, in_5);
  J_K_Flip_Flop j_k_ff_5 (.J(in_5), .clk(and_1_out), .K(not_5_out), .Q(out_15));  // open: Qn, preset, reset
  not not_6 (not_6_out, in_6);
  J_K_Flip_Flop j_k_ff_6 (.J(in_6), .clk(and_1_out), .K(not_6_out), .Q(out_16));  // open: Qn, preset, reset
  not not_7 (not_7_out, in_7);
  J_K_Flip_Flop j_k_ff_7 (.J(in_7), .clk(and_1_out), .K(not_7_out), .Q(out_17));  // open: Qn, preset, reset
  not not_8 (not_8_out, in_8);
  J_K_Flip_Flop j_k_ff_8 (.J(in_8), .clk(and_1_out), .K(not_8_out), .Q(out_18));  // open: Qn, preset, reset
endmodule

module Numero3 (
  input  ADDR1,
  input  ADDR2,
  input  R_W,
  input  in_4,
  input  in_5,
  input  in_6,
  input  in_7,
  input  in_8,
  input  in_9,
  input  in_10,
  input  in_11,
  input  in_12,
  input  in_13,
  input  in_14,
  input  in_15,
  input  in_16,
  input  in_17,
  input  in_18,
  input  in_19,
  output out_20,
  output out_21,
  output out_22,
  output out_23,
  output out_24,
  output out_25,
  output out_26,
  output out_27,
  output out_28,
  output out_29,
  output out_30,
  output out_31,
  output out_32,
  output out_33,
  output out_34,
  output out_35
);

  wire and_1_out, and_2_out, CLK_out;

  Clock CLK (.out(CLK_out));
  and and_1 (and_1_out, ADDR1, R_W, CLK_out);
  _1x8 u_1x8_1 (
    .Ativacao(and_1_out), .INPUT(in_18), .in_2(in_16), .in_3(in_14), .in_4(in_12), .in_5(in_10), .in_6(in_8),
    .in_7(in_6), .in_8(in_4), .out_10(out_20), .out_11(out_21), .out_12(out_22), .out_13(out_23),
    .out_14(out_24), .out_15(out_25), .out_16(out_26), .out_17(out_27));
  and and_2 (and_2_out, ADDR2, R_W, CLK_out);
  _1x8 u_1x8_2 (
    .Ativacao(and_2_out), .INPUT(in_5), .in_2(in_7), .in_3(in_9), .in_4(in_11), .in_5(in_13), .in_6(in_15),
    .in_7(in_17), .in_8(in_19), .out_10(out_28), .out_11(out_29), .out_12(out_30), .out_13(out_31),
    .out_14(out_32), .out_15(out_33), .out_16(out_34), .out_17(out_35));
endmodule

module _1x8 (
  input  INPUT,
  input  in_2,
  input  in_3,
  input  in_4,
  input  in_5,
  input  in_6,
  input  in_7,
  input  in_8,
  input  Ativacao,
  output out_10,
  output out_11,
  output out_12,
  output out_13,
  output out_14,
  output out_15,
  output out_16,
  output out_17
);

  wire not_1_out, not_2_out, not_3_out, not_4_out, not_5_out, not_6_out, not_7_out, not_8_out;

  not not_1 (not_1_out, INPUT);
  J_K_Flip_Flop j_k_ff_1 (.J(INPUT), .clk(Ativacao), .K(not_1_out), .Q(out_10));  // open: Qn, preset, reset
  not not_2 (not_2_out, in_2);
  J_K_Flip_Flop j_k_ff_2 (.J(in_2), .clk(Ativacao), .K(not_2_out), .Q(out_11));  // open: Qn, preset, reset
  J_K_Flip_Flop j_k_ff_3 (.J(in_3), .clk(Ativacao), .K(not_3_out), .Q(out_12));  // open: Qn, preset, reset
  not not_3 (not_3_out, in_3);
  not not_4 (not_4_out, in_4);
  J_K_Flip_Flop j_k_ff_4 (.J(in_4), .clk(Ativacao), .K(not_4_out), .Q(out_13));  // open: Qn, preset, reset
  not not_5 (not_5_out, in_5);
  J_K_Flip_Flop j_k_ff_5 (.J(in_5), .clk(Ativacao), .K(not_5_out), .Q(out_14));  // open: Qn, preset, reset
  not not_6 (not_6_out, in_6);
  J_K_Flip_Flop j_k_ff_6 (.J(in_6), .clk(Ativacao), .K(not_6_out), .Q(out_15));  // open: Qn, preset, reset
  not not_7 (not_7_out, in_7);
  J_K_Flip_Flop j_k_ff_7 (.J(in_7), .clk(Ativacao), .K(not_7_out), .Q(out_16));  // open: Qn, preset, reset
  not not_8 (not_8_out, in_8);
  J_K_Flip_Flop j_k_ff_8 (.J(in_8), .clk(Ativacao), .K(not_8_out), .Q(out_17));  // open: Qn, preset, reset
endmodule

module Numero4 (
  input  ADDR1,
  input  ADDR2,
  input  ADDR3,
  input  ADDR4,
  input  R_W,
  input  in_6,
  input  in_7,
  input  in_8,
  input  in_9,
  input  in_10,
  input  in_11,
  input  in_12,
  input  in_13,
  input  in_14,
  input  in_15,
  input  in_16,
  input  in_17,
  input  in_18,
  input  in_19,
  input  in_20,
  input  in_21,
  input  in_22,
  input  in_23,
  input  in_24,
  input  in_25,
  input  in_26,
  input  in_27,
  input  dois,
  input  quatro,
  input  in_30,
  input  in_31,
  input  in_32,
  input  in_33,
  input  in_34,
  input  in_35,
  input  in_36,
  input  in_37,
  output out_38,
  output out_39,
  output out_40,
  output out_41,
  output out_42,
  output out_43,
  output out_44,
  output out_45,
  output out_46,
  output out_47,
  output out_48,
  output out_49,
  output out_50,
  output out_51,
  output out_52,
  output out_53,
  output out_54,
  output out_55,
  output out_56,
  output out_57,
  output out_58,
  output out_59,
  output out_60,
  output out_61,
  output out_62,
  output out_63,
  output out_64,
  output out_65,
  output out_66,
  output out_67,
  output out_68,
  output out_69
);

  wire and_1_out, and_2_out, and_3_out, and_4_out, CLK_out;

  Clock CLK (.out(CLK_out));
  and and_1 (and_1_out, ADDR1, R_W, CLK_out);
  and and_2 (and_2_out, ADDR2, CLK_out, CLK_out);
  _2x8 u_2x8_1 (
    .in_17(and_1_out), .in_18(and_2_out), .in_2(in_6), .in_3(in_7), .in_4(in_8), .in_5(in_9), .in_6(in_10),
    .in_7(in_11), .in_8(in_12), .in_9(in_13), .out_19(out_38), .out_20(out_39), .out_21(out_40),
    .out_22(out_41), .out_23(out_42), .out_24(out_43), .out_25(out_44), .out_26(out_45), .out_27(out_45),
    .out_28(out_47), .out_29(out_48), .out_30(out_49), .out_31(out_50), .out_32(out_51), .out_33(out_52),
    .out_34(out_53), .in_1(in_22), .in_10(in_24), .in_11(in_26), .in_12(dois), .in_13(in_30), .in_14(in_32),
    .in_15(in_34), .in_16(in_36));
  and and_3 (and_3_out, ADDR3, R_W, CLK_out);
  and and_4 (and_4_out, ADDR4, R_W, CLK_out);
  _2x8 u_2x8_2 (
    .in_17(and_3_out), .in_18(and_4_out), .in_2(in_14), .in_3(in_15), .in_4(in_16), .in_5(in_17),
    .in_6(in_18), .in_7(in_19), .in_8(in_20), .in_9(in_21), .out_19(out_54), .out_20(out_55),
    .out_21(out_56), .out_22(out_57), .out_23(out_58), .out_24(out_59), .out_25(out_60), .out_26(out_61),
    .out_27(out_61), .out_28(out_63), .out_29(out_64), .out_30(out_65), .out_31(out_66), .out_32(out_67),
    .out_33(out_68), .out_34(out_69), .in_1(in_23), .in_10(in_25), .in_11(in_27), .in_12(quatro),
    .in_13(in_31), .in_14(in_33), .in_15(in_35), .in_16(in_37));

  assign out_46 = out_45;
  assign out_62 = out_61;

  // Notes on the sheet:
  //   Bug: se desconectar o r/w desse funciona
  //   um
  //   tres
endmodule

module _2x8 (
  input  in_1,
  input  in_2,
  input  in_3,
  input  in_4,
  input  in_5,
  input  in_6,
  input  in_7,
  input  in_8,
  input  in_9,
  input  in_10,
  input  in_11,
  input  in_12,
  input  in_13,
  input  in_14,
  input  in_15,
  input  in_16,
  input  in_17,
  input  in_18,
  output out_19,
  output out_20,
  output out_21,
  output out_22,
  output out_23,
  output out_24,
  output out_25,
  output out_26,
  output out_27,
  output out_28,
  output out_29,
  output out_30,
  output out_31,
  output out_32,
  output out_33,
  output out_34
);

  _1x8 u_1x8_1 (
    .Ativacao(in_17), .INPUT(in_2), .in_2(in_3), .in_3(in_4), .in_4(in_5), .in_5(in_6), .in_6(in_7),
    .in_7(in_8), .in_8(in_9), .out_10(out_19), .out_11(out_20), .out_12(out_21), .out_13(out_22),
    .out_14(out_23), .out_15(out_24), .out_16(out_25), .out_17(out_26));
  _1x8 u_1x8_2 (
    .Ativacao(in_18), .INPUT(in_1), .in_2(in_10), .in_3(in_11), .in_4(in_12), .in_5(in_13), .in_6(in_14),
    .in_7(in_15), .in_8(in_16), .out_10(out_27), .out_11(out_28), .out_12(out_29), .out_13(out_30),
    .out_14(out_31), .out_15(out_32), .out_16(out_33), .out_17(out_34));
endmodule

module Numero_5 (
  input  ADDR1,
  input  ADDR2,
  input  ADDR3,
  input  ADDR4,
  input  ADDR5,
  input  ADDR6,
  input  ADDR7,
  input  ADDR8,
  input  R_W,
  input  in_10,
  input  in_11,
  input  in_12,
  input  in_13,
  input  in_14,
  input  in_15,
  input  in_16,
  input  in_17,
  input  in_18,
  input  in_19,
  input  in_20,
  input  in_21,
  input  in_22,
  input  in_23,
  input  in_24,
  input  in_25,
  input  in_26,
  input  in_27,
  input  in_28,
  input  in_29,
  input  in_30,
  input  in_31,
  input  in_32,
  input  in_33,
  input  in_34,
  input  in_35,
  input  in_36,
  input  in_37,
  input  in_38,
  input  in_39,
  input  in_40,
  input  in_41,
  input  in_42,
  input  in_43,
  input  in_44,
  input  in_45,
  input  in_46,
  input  in_47,
  input  in_48,
  input  in_49,
  input  in_50,
  input  in_51,
  input  in_52,
  input  in_53,
  input  in_54,
  input  in_55,
  input  in_56,
  input  in_57,
  input  in_58,
  input  in_59,
  input  in_60,
  input  in_61,
  input  in_62,
  input  in_63,
  input  in_64,
  input  in_65,
  input  in_66,
  input  in_67,
  input  in_68,
  input  in_69,
  input  in_70,
  input  in_71,
  input  in_72,
  input  in_73,
  output out_74,
  output out_75,
  output out_76,
  output out_77,
  output out_78,
  output out_79,
  output out_80,
  output out_81,
  output out_82,
  output out_83,
  output out_84,
  output out_85,
  output out_86,
  output out_87,
  output out_88,
  output out_89,
  output out_90,
  output out_91,
  output out_92,
  output out_93,
  output out_94,
  output out_95,
  output out_96,
  output out_97,
  output out_98,
  output out_99,
  output out_100,
  output out_101,
  output out_102,
  output out_103,
  output out_104,
  output out_105,
  output out_106,
  output out_107,
  output out_108,
  output out_109,
  output out_110,
  output out_111,
  output out_112,
  output out_113,
  output out_114,
  output out_115,
  output out_116,
  output out_117,
  output out_118,
  output out_119,
  output out_120,
  output out_121,
  output out_122,
  output out_123,
  output out_124,
  output out_125,
  output out_126,
  output out_127,
  output out_128,
  output out_129,
  output out_130,
  output out_131,
  output out_132,
  output out_133,
  output out_134,
  output out_135,
  output out_136,
  output out_137
);

  wire and_1_out, and_2_out, and_3_out, and_4_out, and_5_out, and_6_out, and_7_out, and_8_out, CLK_out;

  Clock CLK (.out(CLK_out));
  and and_1 (and_1_out, ADDR1, R_W, CLK_out);
  and and_2 (and_2_out, ADDR2, CLK_out, CLK_out);
  and and_3 (and_3_out, ADDR3, CLK_out, CLK_out);
  and and_4 (and_4_out, ADDR4, CLK_out, CLK_out);
  and and_5 (and_5_out, ADDR5, R_W, CLK_out);
  and and_6 (and_6_out, ADDR6, R_W, CLK_out);
  and and_7 (and_7_out, ADDR7, R_W, CLK_out);
  _4x8 u_4x8_1 (
    .in_19(and_1_out), .in_22(and_2_out), .in_27(and_3_out), .in_28(and_4_out), .in_1(in_37), .in_2(in_38),
    .in_3(in_39), .in_4(in_40), .in_5(in_41), .in_6(in_42), .in_7(in_43), .in_8(in_44), .in_9(in_45),
    .in_10(in_46), .in_11(in_47), .in_12(in_48), .in_13(in_49), .in_14(in_50), .in_15(in_51), .in_16(in_52),
    .out_37(out_106), .out_38(out_107), .out_39(out_108), .out_40(out_109), .out_41(out_110),
    .out_42(out_111), .out_43(out_112), .out_44(out_113), .out_45(out_114), .out_46(out_115),
    .out_47(out_116), .out_48(out_117), .out_49(out_118), .out_50(out_119), .out_51(out_120),
    .out_52(out_121), .out_53(out_122), .out_54(out_123), .out_55(out_124), .out_56(out_125),
    .out_57(out_126), .out_58(out_127), .out_59(out_128), .out_60(out_129), .out_61(out_130),
    .out_62(out_131), .out_63(out_132), .out_64(out_133), .out_65(out_134), .out_66(out_134),
    .out_67(out_136), .out_68(out_137), .in_17(in_54), .in_18(in_56), .in_20(in_58), .in_21(in_60),
    .in_23(in_62), .in_24(in_63), .dois(in_64), .quatro(in_65), .in_29(in_66), .in_30(in_67), .in_31(in_68),
    .in_32(in_69), .in_33(in_70), .in_34(in_71), .in_35(in_72), .in_36(in_73));
  and and_8 (and_8_out, ADDR8, R_W, CLK_out);
  _4x8 u_4x8_2 (
    .in_19(and_5_out), .in_22(and_6_out), .in_27(and_7_out), .in_28(and_8_out), .in_1(in_10), .in_2(in_11),
    .in_3(in_12), .in_4(in_13), .in_5(in_14), .in_6(in_15), .in_7(in_16), .in_8(in_17), .in_9(in_18),
    .in_10(in_19), .in_11(in_20), .in_12(in_21), .in_13(in_22), .in_14(in_23), .in_15(in_24), .in_16(in_25),
    .out_37(out_74), .out_38(out_75), .out_39(out_76), .out_40(out_77), .out_41(out_78), .out_42(out_79),
    .out_43(out_80), .out_44(out_81), .out_45(out_82), .out_46(out_83), .out_47(out_84), .out_48(out_85),
    .out_49(out_86), .out_50(out_87), .out_51(out_88), .out_52(out_89), .out_53(out_90), .out_54(out_91),
    .out_55(out_92), .out_56(out_93), .out_57(out_94), .out_58(out_95), .out_59(out_96), .out_60(out_97),
    .out_61(out_98), .out_62(out_99), .out_63(out_100), .out_64(out_101), .out_65(out_102), .out_66(out_102),
    .out_67(out_104), .out_68(out_105), .in_17(in_26), .in_18(in_27), .in_20(in_28), .in_21(in_29),
    .in_23(in_30), .in_24(in_31), .dois(in_32), .quatro(in_33), .in_29(in_34), .in_30(in_35), .in_31(in_36),
    .in_32(in_53), .in_33(in_55), .in_34(in_57), .in_35(in_59), .in_36(in_61));

  assign out_103 = out_102;
  assign out_135 = out_134;
endmodule

module _4x8 (
  input  in_1,
  input  in_2,
  input  in_3,
  input  in_4,
  input  in_5,
  input  in_6,
  input  in_7,
  input  in_8,
  input  in_9,
  input  in_10,
  input  in_11,
  input  in_12,
  input  in_13,
  input  in_14,
  input  in_15,
  input  in_16,
  input  in_17,
  input  in_18,
  input  in_19,
  input  in_20,
  input  in_21,
  input  in_22,
  input  in_23,
  input  in_24,
  input  dois,
  input  quatro,
  input  in_27,
  input  in_28,
  input  in_29,
  input  in_30,
  input  in_31,
  input  in_32,
  input  in_33,
  input  in_34,
  input  in_35,
  input  in_36,
  output out_37,
  output out_38,
  output out_39,
  output out_40,
  output out_41,
  output out_42,
  output out_43,
  output out_44,
  output out_45,
  output out_46,
  output out_47,
  output out_48,
  output out_49,
  output out_50,
  output out_51,
  output out_52,
  output out_53,
  output out_54,
  output out_55,
  output out_56,
  output out_57,
  output out_58,
  output out_59,
  output out_60,
  output out_61,
  output out_62,
  output out_63,
  output out_64,
  output out_65,
  output out_66,
  output out_67,
  output out_68
);

  _2x8 u_2x8_1 (
    .in_17(in_19), .in_18(in_27), .in_2(in_1), .in_3(in_2), .in_4(in_3), .in_5(in_4), .in_6(in_5),
    .in_7(in_6), .in_8(in_7), .in_9(in_8), .out_19(out_37), .out_20(out_38), .out_21(out_39),
    .out_22(out_40), .out_23(out_41), .out_24(out_42), .out_25(out_43), .out_26(out_44), .out_27(out_44),
    .out_28(out_46), .out_29(out_47), .out_30(out_48), .out_31(out_49), .out_32(out_50), .out_33(out_51),
    .out_34(out_52), .in_1(in_17), .in_10(in_20), .in_11(in_23), .in_12(dois), .in_13(in_29), .in_14(in_31),
    .in_15(in_33), .in_16(in_35));
  _2x8 u_2x8_2 (
    .in_17(in_22), .in_18(in_28), .in_2(in_9), .in_3(in_10), .in_4(in_11), .in_5(in_12), .in_6(in_13),
    .in_7(in_14), .in_8(in_15), .in_9(in_16), .out_19(out_53), .out_20(out_54), .out_21(out_55),
    .out_22(out_56), .out_23(out_57), .out_24(out_58), .out_25(out_59), .out_26(out_60), .out_27(out_60),
    .out_28(out_62), .out_29(out_63), .out_30(out_64), .out_31(out_65), .out_32(out_66), .out_33(out_67),
    .out_34(out_68), .in_1(in_18), .in_10(in_21), .in_11(in_24), .in_12(quatro), .in_13(in_30),
    .in_14(in_32), .in_15(in_34), .in_16(in_36));

  assign out_45 = out_44;
  assign out_61 = out_60;

  // Notes on the sheet:
  //   um
  //   tres
endmodule

module Numero6 (
  input  ADDR1,
  input  ADDR2,
  input  ADDR3,
  input  ADDR4,
  input  R_W,
  input  in_6,
  input  in_7,
  input  in_8,
  input  in_9,
  input  in_10,
  input  in_11,
  input  in_12,
  input  in_13,
  input  in_14,
  input  in_15,
  input  in_16,
  input  in_17,
  input  in_18,
  input  in_19,
  input  in_20,
  input  in_21,
  input  in_22,
  input  in_23,
  input  in_24,
  input  in_25,
  input  in_26,
  input  in_27,
  input  in_28,
  input  in_29,
  input  in_30,
  input  in_31,
  input  in_32,
  input  in_33,
  input  in_34,
  input  in_35,
  input  in_36,
  input  in_37,
  output out_38,
  output out_39,
  output out_40,
  output out_41,
  output out_42,
  output out_43,
  output out_44,
  output out_45,
  output out_46,
  output out_47,
  output out_48,
  output out_49,
  output out_50,
  output out_51,
  output out_52,
  output out_53,
  output out_54,
  output out_55,
  output out_56,
  output out_57,
  output out_58,
  output out_59,
  output out_60,
  output out_61,
  output out_62,
  output out_63,
  output out_64,
  output out_65,
  output out_66,
  output out_67,
  output out_68,
  output out_69
);

  wire and_1_out, and_2_out, and_3_out, and_4_out;

  Clock CLK (.out(R_W));
  and and_1 (and_1_out, ADDR1, R_W, R_W);
  and and_2 (and_2_out, ADDR2, R_W, R_W);
  and and_3 (and_3_out, ADDR3, R_W, R_W);
  and and_4 (and_4_out, ADDR4, R_W, R_W);
  _4x8 u_4x8_1 (
    .in_19(and_1_out), .in_22(and_2_out), .in_27(and_3_out), .in_28(and_4_out), .in_1(in_6), .in_2(in_7),
    .in_3(in_8), .in_4(in_9), .in_5(in_10), .in_6(in_11), .in_7(in_12), .in_8(in_13), .in_9(in_14),
    .in_10(in_15), .in_11(in_16), .in_12(in_17), .in_13(in_18), .in_14(in_19), .in_15(in_20), .in_16(in_21),
    .out_37(out_38), .out_38(out_39), .out_39(out_40), .out_40(out_41), .out_41(out_42), .out_42(out_43),
    .out_43(out_44), .out_44(out_45), .out_45(out_46), .out_46(out_47), .out_47(out_48), .out_48(out_49),
    .out_49(out_50), .out_50(out_51), .out_51(out_52), .out_52(out_53), .out_53(out_54), .out_54(out_55),
    .out_55(out_56), .out_56(out_57), .out_57(out_58), .out_58(out_59), .out_59(out_60), .out_60(out_61),
    .out_61(out_62), .out_62(out_63), .out_63(out_64), .out_64(out_65), .out_65(out_66), .out_66(out_66),
    .out_67(out_68), .out_68(out_69), .in_17(in_22), .in_18(in_23), .in_20(in_24), .in_21(in_25),
    .in_23(in_26), .in_24(in_27), .dois(in_28), .quatro(in_29), .in_29(in_30), .in_30(in_31), .in_31(in_32),
    .in_32(in_33), .in_33(in_34), .in_34(in_35), .in_35(in_36), .in_36(in_37));

  assign out_67 = out_66;
endmodule

module _1x16 (
  input  in_1,
  input  in_2,
  input  in_3,
  input  in_4,
  input  in_5,
  input  in_6,
  input  in_7,
  input  in_8,
  input  in_9,
  input  in_10,
  input  in_11,
  input  in_12,
  input  in_13,
  input  in_14,
  input  in_15,
  input  in_16,
  input  in_17,
  output out_18,
  output out_19,
  output out_20,
  output out_21,
  output out_22,
  output out_23,
  output out_24,
  output out_25,
  output out_26,
  output out_27,
  output out_28,
  output out_29,
  output out_30,
  output out_31,
  output out_32,
  output out_33
);

  _1x8 u_1x8_1 (
    .Ativacao(in_1), .INPUT(in_3), .in_2(in_4), .in_3(in_5), .in_4(in_6), .in_5(in_7), .in_6(in_8),
    .in_7(in_9), .in_8(in_10), .out_10(out_18), .out_11(out_19), .out_12(out_20), .out_13(out_21),
    .out_14(out_22), .out_15(out_23), .out_16(out_24), .out_17(out_25));
  _1x8 u_1x8_2 (
    .Ativacao(in_1), .INPUT(in_2), .in_2(in_11), .in_3(in_12), .in_4(in_13), .in_5(in_14), .in_6(in_15),
    .in_7(in_16), .in_8(in_17), .out_10(out_26), .out_11(out_27), .out_12(out_28), .out_13(out_29),
    .out_14(out_30), .out_15(out_31), .out_16(out_32), .out_17(out_33));
endmodule

module Numero7 (
  input  ADDR,
  input  R_W,
  input  in_3,
  input  in_4,
  input  in_5,
  input  in_6,
  input  in_7,
  input  in_8,
  input  in_9,
  input  in_10,
  input  in_11,
  input  in_12,
  input  in_13,
  input  in_14,
  input  in_15,
  input  in_16,
  input  in_17,
  input  [2:0] in_18,
  input  in_19,
  output out_20,
  output out_21,
  output out_22,
  output out_23,
  output out_24,
  output out_25,
  output out_26,
  output out_27,
  output out_28,
  output out_29,
  output out_30,
  output out_31,
  output out_32,
  output out_33,
  output out_34,
  output out_35
);

  wire and_1_out, and_2_out, and_3_out, and_4_out, and_5_out, and_6_out, and_7_out, and_8_out, CLK_out,
       demultiplexer_1_out0, demultiplexer_1_out1, demultiplexer_1_out2, demultiplexer_1_out3,
       demultiplexer_1_out5, demultiplexer_1_out6, demultiplexer_1_out7, multiplexer_1_out;

  Clock CLK (.out(CLK_out));
  Demultiplexer #(.select(3), .enable("false")) demultiplexer_1 (
    .out0(demultiplexer_1_out0), .out1(demultiplexer_1_out1), .out2(demultiplexer_1_out2),
    .out3(demultiplexer_1_out3), .out4(demultiplexer_1_out3), .out5(demultiplexer_1_out5),
    .out6(demultiplexer_1_out6), .out7(demultiplexer_1_out7), .in(ADDR), .sel(in_18));
  and and_1 (and_1_out, demultiplexer_1_out0, R_W, CLK_out);
  Multiplexer #(.select(3), .enable("false")) multiplexer_1 (
    .in0(and_1_out), .in1(and_2_out), .in2(and_3_out), .in3(and_4_out), .in4(and_5_out), .in5(and_6_out),
    .in6(and_7_out), .in7(and_8_out), .out(multiplexer_1_out), .sel(in_18));
  and and_2 (and_2_out, demultiplexer_1_out1, CLK_out, CLK_out);
  and and_3 (and_3_out, demultiplexer_1_out2, CLK_out, CLK_out);
  and and_4 (and_4_out, demultiplexer_1_out3, CLK_out, CLK_out);
  and and_5 (and_5_out, demultiplexer_1_out3, R_W, CLK_out);
  _1x16 u_1x16_1 (
    .in_1(multiplexer_1_out), .in_3(in_3), .in_4(in_4), .in_5(in_5), .in_6(in_6), .in_7(in_7), .in_8(in_8),
    .in_9(in_9), .in_10(in_10), .out_18(out_20), .out_19(out_21), .out_20(out_22), .out_21(out_23),
    .out_22(out_24), .out_23(out_25), .out_24(out_26), .out_25(out_27), .out_26(out_27), .out_27(out_29),
    .out_28(out_30), .out_29(out_31), .out_30(out_32), .out_31(out_33), .out_32(out_34), .out_33(out_35),
    .in_2(in_11), .in_11(in_12), .in_12(in_13), .in_13(in_14), .in_14(in_15), .in_15(in_16), .in_16(in_17),
    .in_17(in_19));
  and and_6 (and_6_out, demultiplexer_1_out5, R_W, CLK_out);
  and and_7 (and_7_out, demultiplexer_1_out6, R_W, CLK_out);
  and and_8 (and_8_out, demultiplexer_1_out7, R_W, CLK_out);

  assign out_28 = out_27;
endmodule
