// Logisim project R02.circ as structural Verilog
module _5a (
  input  \input ,
  input  clr,
  input  L_D,
  input  in_4,
  input  in_5,
  input  in_6,
  input  in_7,
  output out_8,
  output out_9,
  output out_10,
  output out_11
);

  wire and_1_out, and_2_out, and_3_out, and_4_out, clk_out;

  Clock clk (.out(clk_out));
  D_Flip_Flop #(.Pre_Clr_Positions("LEGACY"), .NewFFLayout("false")) d_ff_1 (
    .clk(clk_out), .D(\input ), .Q(out_8), .preset(and_1_out), .reset(clr));  // open: Qn
  and and_1 (and_1_out, L_D, in_4);
  D_Flip_Flop #(.Pre_Clr_Positions("LEGACY"), .NewFFLayout("false")) d_ff_2 (
    .clk(clk_out), .D(out_8), .Q(out_9), .preset(and_2_out), .reset(clr));  // open: Qn
  and and_2 (and_2_out, L_D, in_5);
  D_Flip_Flop #(.Pre_Clr_Positions("LEGACY"), .NewFFLayout("false")) d_ff_3 (
    .clk(clk_out), .D(out_9), .Q(out_10), .preset(and_3_out), .reset(clr));  // open: Qn
  and and_3 (and_3_out, L_D, in_6);
  and and_4 (and_4_out, L_D, in_7);
  D_Flip_Flop #(.Pre_Clr_Positions("LEGACY"), .NewFFLayout("false")) d_ff_4 (
    .clk(clk_out), .D(out_10), .Q(out_11), .preset(and_4_out), .reset(clr));  // open: Qn

  // Notes on the sheet:
  //   a
  //   b
  //   c
  //   d
endmodule

module _5b (
  input  \input ,
  input  clr,
  input  L_D,
  input  in_4,
  input  in_5,
  input  in_6,
  input  in_7,
  output out_8,
  output out_9,
  output out_10,
  output out_11
);

  wire and_1_out, and_2_out, and_3_out, and_4_out, clk_out;

  Clock clk (.out(clk_out));
  D_Flip_Flop #(.Pre_Clr_Positions("LEGACY"), .NewFFLayout("false")) d_ff_1 (
    .clk(clk_out), .D(out_9), .Q(out_8), .preset(and_1_out), .reset(clr));  // open: Qn
  and and_1 (and_1_out, L_D, in_4);
  D_Flip_Flop #(.Pre_Clr_Positions("LEGACY"), .NewFFLayout("false")) d_ff_2 (
    .clk(clk_out), .D(out_10), .Q(out_9), .preset(and_2_out), .reset(clr));  // open: Qn
  and and_2 (and_2_out, L_D, in_5);
  D_Flip_Flop #(.Pre_Clr_Positions("LEGACY"), .NewFFLayout("false")) d_ff_3 (
    .clk(clk_out), .D(out_11), .Q(out_10), .preset(and_3_out), .reset(clr));  // open: Qn
  and and_3 (and_3_out, L_D, in_6);
  and and_4 (and_4_out, L_D, in_7);
  D_Flip_Flop #(.Pre_Clr_Positions("LEGACY"), .NewFFLayout("false")) d_ff_4 (
    .clk(clk_out), .D(\input ), .Q(out_11), .preset(and_4_out), .reset(clr));  // open: Qn

  // Notes on the sheet:
  //   a
  //   b
  //   c
  //   d
endmodule

module _5c (
  input  \input ,
  input  clr,
  input  L_D,
  input  in_4,
  input  in_5,
  input  in_6,
  output out_7,
  output out_8,
  output out_9,
  output out_10
);

  wire and_1_out, and_2_out, and_3_out, clk_out, xor_1_out;

  Clock clk (.out(clk_out));
  D_Flip_Flop #(.Pre_Clr_Positions("LEGACY"), .NewFFLayout("false")) d_ff_1 (
    .clk(clk_out), .D(\input ), .Q(out_7), .preset(xor_1_out), .reset(clr));  // open: Qn
  xor xor_1 (xor_1_out, 1'b1, in_6);
  D_Flip_Flop #(.Pre_Clr_Positions("LEGACY"), .NewFFLayout("false")) d_ff_2 (
    .clk(clk_out), .D(out_7), .Q(out_8), .preset(and_1_out), .reset(clr));  // open: Qn
  and and_1 (and_1_out, L_D, in_4);
  D_Flip_Flop #(.Pre_Clr_Positions("LEGACY"), .NewFFLayout("false")) d_ff_3 (
    .clk(clk_out), .D(out_8), .Q(out_9), .preset(and_2_out), .reset(clr));  // open: Qn
  and and_2 (and_2_out, L_D, in_5);
  and and_3 (and_3_out, L_D, in_6);
  D_Flip_Flop #(.Pre_Clr_Positions("LEGACY"), .NewFFLayout("false")) d_ff_4 (
    .clk(clk_out), .D(out_9), .Q(out_10), .preset(and_3_out), .reset(clr));  // open: Qn

  // Notes on the sheet:
  //   a
  //   b
  //   c
  //   d
endmodule

module _5d (
  input  \input ,
  input  clr,
  input  L_D,
  input  in_4,
  input  in_5,
  input  in_6,
  output out_7,
  output out_8,
  output out_9,
  output out_10
);

  wire and_1_out, and_2_out, and_3_out, clk_out, nand_1_out;

  Clock clk (.out(clk_out));
  D_Flip_Flop #(.Pre_Clr_Positions("LEGACY"), .NewFFLayout("false")) d_ff_1 (
    .clk(clk_out), .D(\input ), .Q(out_7), .preset(nand_1_out), .reset(clr));  // open: Qn
  nand nand_1 (nand_1_out, 1'b0, in_6);
  D_Flip_Flop #(.Pre_Clr_Positions("LEGACY"), .NewFFLayout("false")) d_ff_2 (
    .clk(clk_out), .D(out_7), .Q(out_8), .preset(and_1_out), .reset(clr));  // open: Qn
  and and_1 (and_1_out, L_D, in_4);
  D_Flip_Flop #(.Pre_Clr_Positions("LEGACY"), .NewFFLayout("false")) d_ff_3 (
    .clk(clk_out), .D(out_8), .Q(out_9), .preset(and_2_out), .reset(clr));  // open: Qn
  and and_2 (and_2_out, L_D, in_5);
  and and_3 (and_3_out, L_D, in_6);
  D_Flip_Flop #(.Pre_Clr_Positions("LEGACY"), .NewFFLayout("false")) d_ff_4 (
    .clk(clk_out), .D(out_9), .Q(out_10), .preset(and_3_out), .reset(clr));  // open: Qn

  // Notes on the sheet:
  //   a
  //   b
  //   c
  //   d
endmodule

module _5e (
  input  In,
  input  clear,
  input  LOAD,
  input  in_4,
  input  in_5,
  input  in_6,
  output out_7,
  output out_8,
  output out_9,
  output out_10
);

  wire and_1_out, and_2_out, and_3_out, and_4_out, clock_1_out, not_1_out, not_2_out, not_3_out, not_4_out,
       not_5_out, or_1_out;

  Clock clock_1 (.out(clock_1_out));
  or or_1 (or_1_out, In, out_10);
  not not_1 (not_1_out, or_1_out);
  J_K_Flip_Flop #(.Pre_Clr_Positions("LEGACY"), .NewFFLayout("false")) j_k_ff_1 (
    .J(or_1_out), .clk(clock_1_out), .K(not_1_out), .Q(out_7), .preset(and_1_out), .reset(clear));  // open: Qn
  not not_2 (not_2_out, out_7);
  and and_1 (and_1_out, LOAD, in_4);
  J_K_Flip_Flop #(.Pre_Clr_Positions("LEGACY"), .NewFFLayout("false")) j_k_ff_2 (
    .J(out_7), .clk(clock_1_out), .K(not_2_out), .Q(out_8), .preset(and_2_out), .reset(clear));  // open: Qn
  and and_2 (and_2_out, LOAD, in_5);
  J_K_Flip_Flop #(.Pre_Clr_Positions("LEGACY"), .NewFFLayout("false")) j_k_ff_3 (
    .J(out_8), .clk(clock_1_out), .K(not_3_out), .Q(out_9), .preset(and_3_out), .reset(clear));  // open: Qn
  not not_3 (not_3_out, out_8);
  and and_3 (and_3_out, LOAD, in_6);
  not not_4 (not_4_out, out_9);
  and and_4 (and_4_out, LOAD, not_5_out);
  J_K_Flip_Flop #(.Pre_Clr_Positions("LEGACY"), .NewFFLayout("false")) j_k_ff_4 (
    .J(out_9), .clk(clock_1_out), .K(not_4_out), .Q(out_10), .preset(and_4_out), .reset(clear));  // open: Qn
  not not_5 (not_5_out, out_10);

  // Notes on the sheet:
  //   a
  //   b
  //   c
  //   d
endmodule

module _6 (
  input  [2:0] in_1,
  input  In,
  input  clear,
  output [2:0] out_4
);

  wire and_1_out, and_2_out, and_3_out, clock_1_out, j_k_ff_1_q, j_k_ff_2_q, j_k_ff_3_q, j_k_ff_4_q,
       not_1_out, not_2_out, not_3_out, not_4_out, not_5_out, not_6_out, not_7_out, or_1_out, or_2_out;

  Clock clock_1 (.out(clock_1_out));
  or or_1 (or_1_out, In, j_k_ff_4_q);
  not not_1 (not_1_out, or_1_out);
  and and_1 (and_1_out, j_k_ff_1_q, j_k_ff_2_q, j_k_ff_3_q);
  J_K_Flip_Flop #(.Pre_Clr_Positions("LEGACY"), .NewFFLayout("false")) j_k_ff_1 (
    .J(or_1_out), .clk(clock_1_out), .K(not_1_out), .Q(j_k_ff_1_q), .reset(clear));  // open: Qn, preset
  not not_2 (not_2_out, j_k_ff_1_q);
  Counter #(.width(3), .max('h7)) counter_1 (
    .D(in_1), .Q(out_4), .clk(and_2_out));  // open: load, count, carry, clr, preset, down
  and and_2 (and_2_out, clock_1_out, or_2_out);
  or or_2 (or_2_out, and_1_out, and_3_out);
  and and_3 (and_3_out, not_4_out, not_5_out, not_3_out);
  not not_3 (not_3_out, j_k_ff_3_q);
  not not_4 (not_4_out, j_k_ff_1_q);
  not not_5 (not_5_out, j_k_ff_2_q);
  J_K_Flip_Flop #(.Pre_Clr_Positions("LEGACY"), .NewFFLayout("false")) j_k_ff_2 (
    .J(j_k_ff_1_q), .clk(clock_1_out), .K(not_2_out), .Q(j_k_ff_2_q), .reset(clear));  // open: Qn, preset
  not not_6 (not_6_out, j_k_ff_2_q);
  J_K_Flip_Flop #(.Pre_Clr_Positions("LEGACY"), .NewFFLayout("false")) j_k_ff_3 (
    .J(j_k_ff_2_q), .clk(clock_1_out), .K(not_6_out), .Q(j_k_ff_3_q), .reset(clear));  // open: Qn, preset
  not not_7 (not_7_out, j_k_ff_3_q);
  J_K_Flip_Flop #(.Pre_Clr_Positions("LEGACY"), .NewFFLayout("false")) j_k_ff_4 (
    .J(j_k_ff_3_q), .clk(clock_1_out), .K(not_7_out), .Q(j_k_ff_4_q), .reset(clear));  // open: Qn, preset
endmodule

module _7 (
  input  [2:0] in_1,
  input  In,
  input  clear,
  output [2:0] out_4
);

  wire and_1_out, and_2_out, and_3_out, clock_1_out, j_k_ff_1_q, j_k_ff_2_q, j_k_ff_3_q, j_k_ff_4_q,
       not_1_out, not_2_out, not_3_out, not_4_out, not_5_out, not_6_out, not_7_out, or_1_out, or_2_out;

  Clock clock_1 (.out(clock_1_out));
  or or_1 (or_1_out, In, j_k_ff_4_q);
  not not_1 (not_1_out, or_1_out);
  and and_1 (and_1_out, j_k_ff_1_q, j_k_ff_2_q, j_k_ff_3_q);
  J_K_Flip_Flop #(.Pre_Clr_Positions("LEGACY"), .NewFFLayout("false")) j_k_ff_1 (
    .J(or_1_out), .clk(clock_1_out), .K(not_1_out), .Q(j_k_ff_1_q), .reset(clear));  // open: Qn, preset
  not not_2 (not_2_out, j_k_ff_1_q);
  Counter #(.width(3), .max('h7), .trigger("falling")) counter_1 (
    .D(in_1), .Q(out_4), .clk(and_2_out));  // open: load, count, carry, clr, preset, down
  and and_2 (and_2_out, clock_1_out, or_2_out);
  or or_2 (or_2_out, and_1_out, and_3_out);
  and and_3 (and_3_out, not_4_out, not_3_out, not_5_out);
  not not_3 (not_3_out, j_k_ff_2_q);
  not not_4 (not_4_out, j_k_ff_1_q);
  not not_5 (not_5_out, j_k_ff_3_q);
  J_K_Flip_Flop #(.Pre_Clr_Positions("LEGACY"), .NewFFLayout("false")) j_k_ff_2 (
    .J(j_k_ff_1_q), .clk(clock_1_out), .K(not_2_out), .Q(j_k_ff_2_q), .reset(clear));  // open: Qn, preset
  not not_6 (not_6_out, j_k_ff_2_q);
  J_K_Flip_Flop #(.Pre_Clr_Positions("LEGACY"), .NewFFLayout("false")) j_k_ff_3 (
    .J(j_k_ff_2_q), .clk(clock_1_out), .K(not_6_out), .Q(j_k_ff_3_q), .reset(clear));  // open: Qn, preset
  not not_7 (not_7_out, j_k_ff_3_q);
  J_K_Flip_Flop #(.Pre_Clr_Positions("LEGACY"), .NewFFLayout("false")) j_k_ff_4 (
    .J(j_k_ff_3_q), .clk(clock_1_out), .K(not_7_out), .Q(j_k_ff_4_q), .reset(clear));  // open: Qn, preset

  // Notes on the sheet:
  //   Agora o contador esta na borda de descida
endmodule

module _4a (
  input  a,
  input  b,
  input  c,
  output out_4
);

  wire and_1_out, and_2_out, clock_1_out, not_1_out, not_2_out, or_1_out;

  not not_1 (not_1_out, b);
  not not_2 (not_2_out, c);
  and and_1 (and_1_out, c, not_1_out);
  or or_1 (or_1_out, and_1_out, and_2_out);
  and and_2 (and_2_out, a, not_2_out);
  Clock clock_1 (.out(clock_1_out));
  D_Flip_Flop #(.Pre_Clr_Positions("LEGACY"), .NewFFLayout("false")) d_ff_1 (
    .clk(clock_1_out), .D(or_1_out), .Q(out_4));  // open: Qn, preset, reset
endmodule

module _4b (
  input  a,
  input  b,
  input  c,
  output out_4
);

  wire and_1_out, and_2_out, clock_1_out, not_1_out, not_2_out, not_3_out;

  not not_1 (not_1_out, a);
  not not_2 (not_2_out, b);
  not not_3 (not_3_out, c);
  and and_1 (and_1_out, not_1_out, b, c);
  and and_2 (and_2_out, a, not_2_out, c);
  Clock clock_1 (.out(clock_1_out));
  J_K_Flip_Flop #(.Pre_Clr_Positions("LEGACY"), .NewFFLayout("false")) j_k_ff_1 (
    .J(and_1_out), .clk(clock_1_out), .K(and_2_out), .Q(out_4));  // open: Qn, preset, reset
endmodule

module _4c (
  input  a,
  input  b,
  input  c,
  output out_4
);

  wire and_1_out, and_2_out, clock_1_out, not_1_out, not_2_out, not_3_out, or_1_out;

  not not_1 (not_1_out, b);
  not not_2 (not_2_out, a);
  not not_3 (not_3_out, c);
  and and_1 (and_1_out, not_2_out, b, c);
  and and_2 (and_2_out, a, not_1_out, c);
  Clock clock_1 (.out(clock_1_out));
  or or_1 (or_1_out, and_1_out, and_2_out);
  T_Flip_Flop #(.Pre_Clr_Positions("LEGACY"), .NewFFLayout("false")) t_ff_1 (
    .clk(clock_1_out), .T(or_1_out), .Q(out_4));  // open: Qn, preset, reset
endmodule

module _4d (
  input  a,
  input  b,
  input  c,
  output out_4
);

  wire and_1_out, and_2_out, clock_1_out, not_1_out, not_2_out, not_3_out;

  not not_1 (not_1_out, a);
  not not_2 (not_2_out, b);
  not not_3 (not_3_out, c);
  and and_1 (and_1_out, not_1_out, not_2_out, c);
  and and_2 (and_2_out, a, b, c);
  Clock clock_1 (.out(clock_1_out));
  S_R_Flip_Flop #(.Pre_Clr_Positions("LEGACY"), .NewFFLayout("false")) s_r_ff_1 (
    .S(and_1_out), .clk(clock_1_out), .R(and_2_out), .Q(out_4));  // open: Qn, preset, reset
endmodule

module _4e (
  input  a,
  input  b,
  input  c,
  output out_4
);

  wire and_1_out, and_2_out, clock_1_out, not_1_out, not_2_out, not_3_out, or_1_out;

  not not_1 (not_1_out, b);
  not not_2 (not_2_out, a);
  not not_3 (not_3_out, c);
  and and_1 (and_1_out, not_2_out, not_1_out, c);
  and and_2 (and_2_out, a, b, c);
  Clock clock_1 (.out(clock_1_out));
  or or_1 (or_1_out, and_1_out, and_2_out);
  T_Flip_Flop #(.Pre_Clr_Positions("LEGACY"), .NewFFLayout("false")) t_ff_1 (
    .clk(clock_1_out), .T(or_1_out), .Q(out_4));  // open: Qn, preset, reset
endmodule
