// Logisim project Guia_13.circ as structural Verilog
module Numero1 (
  input  In,
  input  clear,
  output out_3,
  output out_4,
  output out_5,
  output out_6,
  output out_7,
  output out_8
);

  wire j_k_ff_2_q, j_k_ff_3_q, j_k_ff_4_q, j_k_ff_5_q, j_k_ff_6_q, Pulso_p1;

  // ProgrammableGenerator Pulso: pin names not known; wires that end beside it: Pulso_p1
  J_K_Flip_Flop #(.Pre_Clr_Positions("LEGACY"), .NewFFLayout("false")) j_k_ff_1 (
    .J(In), .clk(j_k_ff_2_q), .K(In), .Qn(out_3), .reset(clear));  // open: Q, preset
  J_K_Flip_Flop #(.Pre_Clr_Positions("LEGACY"), .NewFFLayout("false")) j_k_ff_2 (
    .J(In), .clk(j_k_ff_3_q), .K(In), .Q(j_k_ff_2_q), .Qn(out_4), .reset(clear));  // open: preset
  J_K_Flip_Flop #(.Pre_Clr_Positions("LEGACY"), .NewFFLayout("false")) j_k_ff_3 (
    .J(In), .clk(j_k_ff_4_q), .K(In), .Q(j_k_ff_3_q), .Qn(out_5), .reset(clear));  // open: preset
  J_K_Flip_Flop #(.Pre_Clr_Positions("LEGACY"), .NewFFLayout("false")) j_k_ff_4 (
    .J(In), .clk(j_k_ff_5_q), .K(In), .Q(j_k_ff_4_q), .Qn(out_6), .reset(clear));  // open: preset
  J_K_Flip_Flop #(.Pre_Clr_Positions("LEGACY"), .NewFFLayout("false")) j_k_ff_5 (
    .J(In), .clk(j_k_ff_6_q), .K(In), .Q(j_k_ff_5_q), .Qn(out_7), .reset(clear));  // open: preset
  J_K_Flip_Flop #(.Pre_Clr_Positions("LEGACY"), .NewFFLayout("false")) j_k_ff_6 (
    .J(In), .clk(Pulso_p1), .K(In), .Q(j_k_ff_6_q), .Qn(out_8), .reset(clear));  // open: preset

  // Notes on the sheet:
  //   o pulso so ocorre no primeiro jk
endmodule

module Numero2 (
  input  In,
  input  pulse,
  input  clear,
  output out_4,
  output out_5,
  output out_6,
  output out_7,
  output out_8,
  output out_9
);

  J_K_Flip_Flop #(.Pre_Clr_Positions("LEGACY"), .NewFFLayout("false")) j_k_ff_1 (
    .J(In), .clk(out_5), .K(In), .Qn(out_4), .reset(clear));  // open: Q, preset
  J_K_Flip_Flop #(.Pre_Clr_Positions("LEGACY"), .NewFFLayout("false")) j_k_ff_2 (
    .J(In), .clk(out_6), .K(In), .Qn(out_5), .reset(clear));  // open: Q, preset
  J_K_Flip_Flop #(.Pre_Clr_Positions("LEGACY"), .NewFFLayout("false")) j_k_ff_3 (
    .J(In), .clk(out_7), .K(In), .Qn(out_6), .reset(clear));  // open: Q, preset
  J_K_Flip_Flop #(.Pre_Clr_Positions("LEGACY"), .NewFFLayout("false")) j_k_ff_4 (
    .J(In), .clk(out_8), .K(In), .Qn(out_7), .reset(clear));  // open: Q, preset
  J_K_Flip_Flop #(.Pre_Clr_Positions("LEGACY"), .NewFFLayout("false")) j_k_ff_5 (
    .J(In), .clk(out_9), .K(In), .Qn(out_8), .reset(clear));  // open: Q, preset
  J_K_Flip_Flop #(.Pre_Clr_Positions("LEGACY"), .NewFFLayout("false")) j_k_ff_6 (
    .J(In), .clk(pulse), .K(In), .Qn(out_9), .reset(clear));  // open: Q, preset
endmodule

module Numero3 (
  input  In,
  input  pulse,
  input  clear,
  output out_4,
  output out_5,
  output out_6,
  output out_7
);

  wire j_k_ff_1_qn, j_k_ff_2_qn, j_k_ff_3_qn, nand_1_out, nand_2_out, not_1_out, not_2_out, not_3_out;

  not not_1 (not_1_out, clear);
  nand nand_1 (nand_1_out, not_2_out, out_6, not_3_out, out_4);
  nand nand_2 (nand_2_out, not_1_out, nand_1_out);
  not not_2 (not_2_out, out_7);
  not not_3 (not_3_out, out_5);
  J_K_Flip_Flop #(.Pre_Clr_Positions("LEGACY"), .NewFFLayout("false")) j_k_ff_1 (
    .J(In), .clk(pulse), .K(In), .Q(out_7), .Qn(j_k_ff_1_qn), .reset(nand_2_out));  // open: preset
  J_K_Flip_Flop #(.Pre_Clr_Positions("LEGACY"), .NewFFLayout("false")) j_k_ff_2 (
    .J(In), .clk(j_k_ff_1_qn), .K(In), .Q(out_6), .Qn(j_k_ff_2_qn), .reset(nand_2_out));  // open: preset
  J_K_Flip_Flop #(.Pre_Clr_Positions("LEGACY"), .NewFFLayout("false")) j_k_ff_3 (
    .J(In), .clk(j_k_ff_2_qn), .K(In), .Q(out_5), .Qn(j_k_ff_3_qn), .reset(nand_2_out));  // open: preset
  J_K_Flip_Flop #(.Pre_Clr_Positions("LEGACY"), .NewFFLayout("false")) j_k_ff_4 (
    .J(In), .clk(j_k_ff_3_qn), .K(In), .Q(out_4), .reset(nand_2_out));  // open: Qn, preset
endmodule

module Numero4 (
  input  In,
  input  pulse,
  output out_3,
  output out_4,
  output out_5,
  output out_6
);

  wire and_1_out, j_k_ff_1_qn, j_k_ff_2_qn, j_k_ff_3_qn, j_k_ff_4_qn, not_1_out, not_2_out, not_3_out,
       or_1_out;

  and and_1 (and_1_out, not_2_out, j_k_ff_2_qn, not_3_out, j_k_ff_4_qn);
  not not_1 (not_1_out, In);
  or or_1 (or_1_out, not_1_out, and_1_out);
  not not_2 (not_2_out, j_k_ff_1_qn);
  not not_3 (not_3_out, j_k_ff_3_qn);
  J_K_Flip_Flop #(.Pre_Clr_Positions("LEGACY"), .NewFFLayout("false")) j_k_ff_1 (
    .J(In), .clk(pulse), .K(In), .Q(out_6), .Qn(j_k_ff_1_qn), .preset(or_1_out));  // open: reset
  J_K_Flip_Flop #(.Pre_Clr_Positions("LEGACY"), .NewFFLayout("false")) j_k_ff_2 (
    .J(In), .clk(out_6), .K(In), .Q(out_5), .Qn(j_k_ff_2_qn), .preset(or_1_out));  // open: reset
  J_K_Flip_Flop #(.Pre_Clr_Positions("LEGACY"), .NewFFLayout("false")) j_k_ff_3 (
    .J(In), .clk(out_5), .K(In), .Q(out_4), .Qn(j_k_ff_3_qn), .preset(or_1_out));  // open: reset
  J_K_Flip_Flop #(.Pre_Clr_Positions("LEGACY"), .NewFFLayout("false")) j_k_ff_4 (
    .J(In), .clk(out_4), .K(In), .Q(out_3), .Qn(j_k_ff_4_qn), .preset(or_1_out));  // open: reset
endmodule

module Numero5 (
  input  clk,
  input  pulse,
  input  clear
);

  wire t_ff_1_q, t_ff_2_q, t_ff_3_q, t_ff_3_qn;

  T_Flip_Flop #(.Pre_Clr_Positions("LEGACY"), .NewFFLayout("false")) t_ff_1 (
    .clk(clk), .T(pulse), .Q(t_ff_1_q), .reset(clear));  // open: Qn, preset
  T_Flip_Flop #(.Pre_Clr_Positions("LEGACY"), .NewFFLayout("false")) t_ff_2 (
    .clk(clk), .T(t_ff_1_q), .Q(t_ff_2_q), .reset(clear));  // open: Qn, preset
  T_Flip_Flop #(.Pre_Clr_Positions("LEGACY"), .NewFFLayout("false")) t_ff_3 (
    .clk(clk), .T(t_ff_2_q), .Q(t_ff_3_q), .Qn(t_ff_3_qn), .reset(clear));  // open: preset
  T_Flip_Flop #(.Pre_Clr_Positions("LEGACY"), .NewFFLayout("false")) t_ff_4 (
    .clk(clk), .T(t_ff_3_q), .reset(clear));  // open: Q, Qn, preset
endmodule

module Numero6 (
  input  In,
  input  clear,
  output out_3,
  output out_4,
  output out_5,
  output out_6,
  output out_7,
  output out_8
);

  wire not_1_out, not_2_out, not_3_out, not_4_out, not_5_out, not_6_out, or_1_out, Pulso_p1;

  // ProgrammableGenerator Pulso: pin names not known; wires that end beside it: Pulso_p1
  J_K_Flip_Flop #(.Pre_Clr_Positions("LEGACY"), .NewFFLayout("false")) j_k_ff_1 (
    .J(In), .clk(Pulso_p1), .K(not_1_out), .Q(out_3), .reset(or_1_out));  // open: Qn, preset
  not not_1 (not_1_out, In);
  or or_1 (or_1_out, clear, out_8);
  not not_2 (not_2_out, out_3);
  J_K_Flip_Flop #(.Pre_Clr_Positions("LEGACY"), .NewFFLayout("false")) j_k_ff_2 (
    .J(out_3), .clk(Pulso_p1), .K(not_2_out), .Q(out_4), .reset(or_1_out));  // open: Qn, preset
  not not_3 (not_3_out, out_4);
  J_K_Flip_Flop #(.Pre_Clr_Positions("LEGACY"), .NewFFLayout("false")) j_k_ff_3 (
    .J(out_4), .clk(Pulso_p1), .K(not_3_out), .Q(out_5), .reset(or_1_out));  // open: Qn, preset
  not not_4 (not_4_out, out_5);
  J_K_Flip_Flop #(.Pre_Clr_Positions("LEGACY"), .NewFFLayout("false")) j_k_ff_4 (
    .J(out_5), .clk(Pulso_p1), .K(not_4_out), .Q(out_6), .reset(or_1_out));  // open: Qn, preset
  not not_5 (not_5_out, out_6);
  J_K_Flip_Flop #(.Pre_Clr_Positions("LEGACY"), .NewFFLayout("false")) j_k_ff_5 (
    .J(out_6), .clk(Pulso_p1), .K(not_5_out), .Q(out_7), .reset(or_1_out));  // open: Qn, preset
  not not_6 (not_6_out, out_7);
  J_K_Flip_Flop #(.Pre_Clr_Positions("LEGACY"), .NewFFLayout("false")) j_k_ff_6 (
    .J(out_7), .clk(Pulso_p1), .K(not_6_out), .Q(out_8), .reset(or_1_out));  // open: Qn, preset
endmodule

module Numero7 (
  input  In,
  input  clear,
  output out_3,
  output out_4,
  output out_5,
  output out_6,
  output out_7,
  output out_8
);

  wire j_k_ff_6_qn, not_1_out, not_2_out, not_3_out, not_4_out, not_5_out, not_6_out, or_1_out, Pulso_p1;

  // ProgrammableGenerator Pulso: pin names not known; wires that end beside it: Pulso_p1
  or or_1 (or_1_out, In, j_k_ff_6_qn);
  J_K_Flip_Flop #(.Pre_Clr_Positions("LEGACY"), .NewFFLayout("false")) j_k_ff_1 (
    .J(or_1_out), .clk(Pulso_p1), .K(not_1_out), .Q(out_3), .reset(clear));  // open: Qn, preset
  not not_1 (not_1_out, or_1_out);
  not not_2 (not_2_out, out_3);
  J_K_Flip_Flop #(.Pre_Clr_Positions("LEGACY"), .NewFFLayout("false")) j_k_ff_2 (
    .J(out_3), .clk(Pulso_p1), .K(not_2_out), .Q(out_4), .reset(clear));  // open: Qn, preset
  not not_3 (not_3_out, out_4);
  J_K_Flip_Flop #(.Pre_Clr_Positions("LEGACY"), .NewFFLayout("false")) j_k_ff_3 (
    .J(out_4), .clk(Pulso_p1), .K(not_3_out), .Q(out_5), .reset(clear));  // open: Qn, preset
  not not_4 (not_4_out, out_5);
  J_K_Flip_Flop #(.Pre_Clr_Positions("LEGACY"), .NewFFLayout("false")) j_k_ff_4 (
    .J(out_5), .clk(Pulso_p1), .K(not_4_out), .Q(out_6), .reset(clear));  // open: Qn, preset
  not not_5 (not_5_out, out_6);
  J_K_Flip_Flop #(.Pre_Clr_Positions("LEGACY"), .NewFFLayout("false")) j_k_ff_5 (
    .J(out_6), .clk(Pulso_p1), .K(not_5_out), .Q(out_7), .reset(clear));  // open: Qn, preset
  not not_6 (not_6_out, out_7);
  J_K_Flip_Flop #(.Pre_Clr_Positions("LEGACY"), .NewFFLayout("false")) j_k_ff_6 (
    .J(out_7), .clk(Pulso_p1), .K(not_6_out), .Q(out_8), .Qn(j_k_ff_6_qn), .reset(clear));  // open: preset
endmodule
