// Logisim project Guia_14.circ as structural Verilog
module Numero1 (
  input  \input ,
  input  clr,
  input  L_D,
  input  in_4,
  input  in_5,
  input  in_6,
  input  in_7,
  input  in_8,
  output out_9,
  output out_10,
  output out_11,
  output out_12,
  output out_13
);

  wire and_1_out, and_2_out, and_3_out, and_4_out, and_5_out, clk_out;

  Clock clk (.out(clk_out));
  D_Flip_Flop #(.Pre_Clr_Positions("LEGACY"), .NewFFLayout("false")) d_ff_1 (
    .clk(clk_out), .D(out_10), .Q(out_9), .preset(and_1_out), .reset(clr));  // open: Qn
  and and_1 (and_1_out, L_D, in_4);
  D_Flip_Flop #(.Pre_Clr_Positions("LEGACY"), .NewFFLayout("false")) d_ff_2 (
    .clk(clk_out), .D(out_11), .Q(out_10), .preset(and_2_out), .reset(clr));  // open: Qn
  and and_2 (and_2_out, L_D, in_5);
  and and_3 (and_3_out, L_D, in_6);
  D_Flip_Flop #(.Pre_Clr_Positions("LEGACY"), .NewFFLayout("false")) d_ff_3 (
    .clk(clk_out), .D(out_12), .Q(out_11), .preset(and_3_out), .reset(clr));  // open: Qn
  and and_4 (and_4_out, L_D, in_7);
  D_Flip_Flop #(.Pre_Clr_Positions("LEGACY"), .NewFFLayout("false")) d_ff_4 (
    .clk(clk_out), .D(out_13), .Q(out_12), .preset(and_4_out), .reset(clr));  // open: Qn
  and and_5 (and_5_out, L_D, in_8);
  D_Flip_Flop #(.Pre_Clr_Positions("LEGACY"), .NewFFLayout("false")) d_ff_5 (
    .clk(clk_out), .D(\input ), .Q(out_13), .preset(and_5_out), .reset(clr));  // open: Qn
endmodule

module Numero2 (
  input  \input ,
  input  clr,
  input  L_D,
  output out_4,
  output out_5,
  output out_6,
  output out_7,
  output out_8
);

  wire clk_out;

  Clock clk (.out(clk_out));
  D_Flip_Flop #(.Pre_Clr_Positions("LEGACY"), .NewFFLayout("false")) d_ff_1 (
    .clk(clk_out), .D(out_5), .Q(out_4), .preset(L_D), .reset(clr));  // open: Qn
  D_Flip_Flop #(.Pre_Clr_Positions("LEGACY"), .NewFFLayout("false")) d_ff_2 (
    .clk(clk_out), .D(out_6), .Q(out_5), .preset(L_D), .reset(clr));  // open: Qn
  D_Flip_Flop #(.Pre_Clr_Positions("LEGACY"), .NewFFLayout("false")) d_ff_3 (
    .clk(clk_out), .D(out_7), .Q(out_6), .preset(L_D), .reset(clr));  // open: Qn
  D_Flip_Flop #(.Pre_Clr_Positions("LEGACY"), .NewFFLayout("false")) d_ff_4 (
    .clk(clk_out), .D(out_8), .Q(out_7), .preset(L_D), .reset(clr));  // open: Qn
  D_Flip_Flop #(.Pre_Clr_Positions("LEGACY"), .NewFFLayout("false")) d_ff_5 (
    .clk(clk_out), .D(\input ), .Q(out_8), .preset(L_D), .reset(clr));  // open: Qn
endmodule

module Numero_3 (
  input  In,
  input  clear,
  output out_3,
  output out_4,
  output out_5,
  output out_6,
  output out_7
);

  wire clock_1_out, not_1_out, not_2_out, not_3_out, not_4_out, not_5_out, or_1_out;

  Clock clock_1 (.out(clock_1_out));
  or or_1 (or_1_out, In, out_7);
  not not_1 (not_1_out, or_1_out);
  J_K_Flip_Flop #(.Pre_Clr_Positions("LEGACY"), .NewFFLayout("false")) j_k_ff_1 (
    .J(or_1_out), .clk(clock_1_out), .K(not_1_out), .Q(out_3), .reset(clear));  // open: Qn, preset
  not not_2 (not_2_out, out_3);
  J_K_Flip_Flop #(.Pre_Clr_Positions("LEGACY"), .NewFFLayout("false")) j_k_ff_2 (
    .J(out_3), .clk(clock_1_out), .K(not_2_out), .Q(out_4), .reset(clear));  // open: Qn, preset
  J_K_Flip_Flop #(.Pre_Clr_Positions("LEGACY"), .NewFFLayout("false")) j_k_ff_3 (
    .J(out_4), .clk(clock_1_out), .K(not_3_out), .Q(out_5), .reset(clear));  // open: Qn, preset
  not not_3 (not_3_out, out_4);
  J_K_Flip_Flop #(.Pre_Clr_Positions("LEGACY"), .NewFFLayout("false")) j_k_ff_4 (
    .J(out_5), .clk(clock_1_out), .K(not_4_out), .Q(out_6), .reset(clear));  // open: Qn, preset
  not not_4 (not_4_out, out_5);
  not not_5 (not_5_out, out_6);
  J_K_Flip_Flop #(.Pre_Clr_Positions("LEGACY"), .NewFFLayout("false")) j_k_ff_5 (
    .J(out_6), .clk(clock_1_out), .K(not_5_out), .Q(out_7), .reset(clear));  // open: Qn, preset
endmodule

module Numero4 (
  input  In,
  input  clear,
  input  L_D,
  output out_4,
  output out_5,
  output out_6,
  output out_7,
  output out_8
);

  wire clock_1_out, d_ff_1_qn, or_1_out;

  Clock clock_1 (.out(clock_1_out));
  or or_1 (or_1_out, d_ff_1_qn, In);
  D_Flip_Flop #(.Pre_Clr_Positions("LEGACY"), .NewFFLayout("false")) d_ff_1 (
    .clk(clock_1_out), .D(out_5), .Q(out_4), .Qn(d_ff_1_qn), .preset(L_D), .reset(clear));
  D_Flip_Flop #(.Pre_Clr_Positions("LEGACY"), .NewFFLayout("false")) d_ff_2 (
    .clk(clock_1_out), .D(out_6), .Q(out_5), .preset(L_D), .reset(clear));  // open: Qn
  D_Flip_Flop #(.Pre_Clr_Positions("LEGACY"), .NewFFLayout("false")) d_ff_3 (
    .clk(clock_1_out), .D(out_7), .Q(out_6), .preset(L_D), .reset(clear));  // open: Qn
  D_Flip_Flop #(.Pre_Clr_Positions("LEGACY"), .NewFFLayout("false")) d_ff_4 (
    .clk(clock_1_out), .D(out_8), .Q(out_7), .preset(L_D), .reset(clear));  // open: Qn
  D_Flip_Flop #(.Pre_Clr_Positions("LEGACY"), .NewFFLayout("false")) d_ff_5 (
    .clk(clock_1_out), .D(or_1_out), .Q(out_8), .preset(L_D), .reset(clear));  // open: Qn
endmodule

module Numero5 (
  input  clr,
  input  L_D,
  input  in_3,
  input  in_4,
  input  in_5,
  input  in_6,
  input  in_7,
  output out_8,
  output out_9,
  output out_10,
  output out_11,
  output out_12
);

  wire and_1_out, and_2_out, and_3_out, and_4_out, and_5_out, clk_out;

  Clock clk (.out(clk_out));
  D_Flip_Flop #(.Pre_Clr_Positions("LEGACY"), .NewFFLayout("false")) d_ff_1 (
    .clk(clk_out), .D(1'b0), .Q(out_8), .preset(and_1_out), .reset(clr));  // open: Qn
  and and_1 (and_1_out, L_D, in_3);
  D_Flip_Flop #(.Pre_Clr_Positions("LEGACY"), .NewFFLayout("false")) d_ff_2 (
    .clk(clk_out), .D(out_8), .Q(out_9), .preset(and_2_out), .reset(clr));  // open: Qn
  and and_2 (and_2_out, L_D, in_4);
  D_Flip_Flop #(.Pre_Clr_Positions("LEGACY"), .NewFFLayout("false")) d_ff_3 (
    .clk(clk_out), .D(out_9), .Q(out_10), .preset(and_3_out), .reset(clr));  // open: Qn
  and and_3 (and_3_out, L_D, in_5);
  D_Flip_Flop #(.Pre_Clr_Positions("LEGACY"), .NewFFLayout("false")) d_ff_4 (
    .clk(clk_out), .D(out_10), .Q(out_11), .preset(and_4_out), .reset(clr));  // open: Qn
  and and_4 (and_4_out, L_D, in_6);
  and and_5 (and_5_out, L_D, in_7);
  D_Flip_Flop #(.Pre_Clr_Positions("LEGACY"), .NewFFLayout("false")) d_ff_5 (
    .clk(clk_out), .D(out_11), .Q(out_12), .preset(and_5_out), .reset(clr));  // open: Qn
endmodule

module Numero6 (
  input  In,
  input  clear,
  input  L_D,
  output out_4,
  output out_5,
  output out_6,
  output out_7,
  output out_8,
  output out_9
);

  wire clock_1_out, or_1_out;

  Clock clock_1 (.out(clock_1_out));
  or or_1 (or_1_out, out_4, In);
  D_Flip_Flop #(.Pre_Clr_Positions("LEGACY"), .NewFFLayout("false")) d_ff_1 (
    .clk(clock_1_out), .D(out_5), .Q(out_4), .preset(L_D), .reset(clear));  // open: Qn
  D_Flip_Flop #(.Pre_Clr_Positions("LEGACY"), .NewFFLayout("false")) d_ff_2 (
    .clk(clock_1_out), .D(out_6), .Q(out_5), .preset(L_D), .reset(clear));  // open: Qn
  D_Flip_Flop #(.Pre_Clr_Positions("LEGACY"), .NewFFLayout("false")) d_ff_3 (
    .clk(clock_1_out), .D(out_7), .Q(out_6), .preset(L_D), .reset(clear));  // open: Qn
  D_Flip_Flop #(.Pre_Clr_Positions("LEGACY"), .NewFFLayout("false")) d_ff_4 (
    .clk(clock_1_out), .D(out_8), .Q(out_7), .preset(L_D), .reset(clear));  // open: Qn
  D_Flip_Flop #(.Pre_Clr_Positions("LEGACY"), .NewFFLayout("false")) d_ff_5 (
    .clk(clock_1_out), .D(out_9), .Q(out_8), .preset(L_D), .reset(clear));  // open: Qn
  D_Flip_Flop #(.Pre_Clr_Positions("LEGACY"), .NewFFLayout("false")) d_ff_6 (
    .clk(clock_1_out), .D(or_1_out), .Q(out_9), .preset(L_D), .reset(clear));  // open: Qn
endmodule

module Numero7 (
  input  In,
  input  clr,
  input  ld,
  output out_4,
  output out_5,
  output out_6,
  output out_7,
  output out_8
);

  wire clock_1_out, j_k_ff_5_qn, not_1_out, not_2_out, not_3_out, not_4_out, not_5_out, or_1_out;

  Clock clock_1 (.out(clock_1_out));
  or or_1 (or_1_out, In, j_k_ff_5_qn);
  J_K_Flip_Flop #(.Pre_Clr_Positions("LEGACY"), .NewFFLayout("false")) j_k_ff_1 (
    .J(or_1_out), .clk(clock_1_out), .K(not_1_out), .Q(out_4), .preset(ld), .reset(clr));  // open: Qn
  not not_1 (not_1_out, or_1_out);
  not not_2 (not_2_out, out_4);
  J_K_Flip_Flop #(.Pre_Clr_Positions("LEGACY"), .NewFFLayout("false")) j_k_ff_2 (
    .J(out_4), .clk(clock_1_out), .K(not_2_out), .Q(out_5), .preset(ld), .reset(clr));  // open: Qn
  not not_3 (not_3_out, out_5);
  J_K_Flip_Flop #(.Pre_Clr_Positions("LEGACY"), .NewFFLayout("false")) j_k_ff_3 (
    .J(out_5), .clk(clock_1_out), .K(not_3_out), .Q(out_6), .preset(ld), .reset(clr));  // open: Qn
  not not_4 (not_4_out, out_6);
  J_K_Flip_Flop #(.Pre_Clr_Positions("LEGACY"), .NewFFLayout("false")) j_k_ff_4 (
    .J(out_6), .clk(clock_1_out), .K(not_4_out), .Q(out_7), .preset(ld), .reset(clr));  // open: Qn
  not not_5 (not_5_out, out_7);
  J_K_Flip_Flop #(.Pre_Clr_Positions("LEGACY"), .NewFFLayout("false")) j_k_ff_5 (
    .J(out_7), .clk(clock_1_out), .K(not_5_out), .Q(out_8), .Qn(j_k_ff_5_qn), .preset(ld), .reset(clr));
endmodule
