// Logisim project Guia5.circ as structural Verilog
module Numero1 (
  input  in_1,
  input  in_2,
  input  in_3,
  input  A,
  input  in_5,
  input  B,
  output out_7,
  output out_8
);

  wire nor_1_out, not_1_out;

  and and_1 (out_7, in_1, not_1_out);
  not not_1 (not_1_out, in_2);
  nor nor_1 (nor_1_out, A, B);
  nor nor_2 (out_8, nor_1_out, B);
  // NAND_Gate nand_1 has open pins: in0=in_3, in1=in_3, out=open
  // NOR_Gate nor_3 has open pins: in0=in_5, in1=in_5, out=open

  // Notes on the sheet:
  //   Numero 1
  //   Tulio Gomes Braga - 802512
  //   Agora somente usando portas NOR
  //   Quando eu ligo o mesmo cabo eu consigo ignorar a porta, ficando somente o not
endmodule

module Numero2 (
  input  A,
  input  B,
  input  A_2,
  input  B_2,
  output out_5,
  output out_6
);

  wire nand_1_out, not_1_out;

  not not_1 (not_1_out, A);
  or or_1 (out_5, not_1_out, B);
  nand nand_1 (nand_1_out, B_2, B_2);
  nand nand_2 (out_6, A_2, nand_1_out);

  // Notes on the sheet:
  //   Numero 2
  //   Tulio Gomes Braga - 802512
  //   Agora somente usando portas Nand
endmodule

module Numero3 (
  input  A,
  input  B,
  input  A_2,
  input  B_2,
  output out_5,
  output out_6
);

  wire nor_1_out, nor_2_out, not_1_out;

  not not_1 (not_1_out, A);
  or or_1 (out_5, not_1_out, B);
  nor nor_1 (nor_1_out, A_2, A_2);
  nor nor_2 (nor_2_out, nor_1_out, B_2);
  nor nor_3 (out_6, nor_2_out, nor_2_out);

  // Notes on the sheet:
  //   Numero 3
  //   Tulio Gomes Braga - 802512
  //   Agora somente usando portas Nor
endmodule

module Numero5 (
  input  in_1,
  input  in_2,
  input  in_3,
  input  in_4,
  output out_5,
  output out_6
);

  wire and_2_out, and_out, nor_1_out, nor_2_out;

  xnor xnor_1 (out_5, in_1, in_2);
  nor nor_1 (nor_1_out, in_4, in_4);
  nor nor_2 (nor_2_out, in_3, in_3);
  nor \and  (and_out, in_3, nor_1_out);
  nor and_2 (and_2_out, nor_2_out, in_4);
  nor nor_3 (out_6, and_out, and_2_out);

  // Notes on the sheet:
  //   Numero 5
  //   Tulio Gomes Braga - 802512
  //   Agora somente usando portas Nor
endmodule

module Numero4 (
  input  A,
  input  B,
  input  A_2,
  input  B_2,
  output out_5,
  output out_6
);

  wire and_1_out, nand_1_out, not_1_out;

  not not_1 (not_1_out, B);
  and and_1 (and_1_out, A, not_1_out);
  not not_2 (out_5, and_1_out);
  nand nand_1 (nand_1_out, B_2, B_2);
  nand nand_2 (out_6, A_2, nand_1_out);

  // Notes on the sheet:
  //   Numero 4
  //   Tulio Gomes Braga - 802512
  //   Agora somente usando portas Nand
endmodule

module Numero6 (
  input  in_1,
  input  in_2,
  input  in_3,
  input  in_4,
  input  in_5,
  input  in_6,
  output out_7,
  output out_8
);

  wire nand_1_out, nand_2_out, nand_3_out, nand_4_out, nand_6_out, nand_7_out;

  xor xor_1 (out_7, in_2, in_4);
  nand nand_1 (nand_1_out, in_5, in_5);
  nand nand_2 (nand_2_out, in_6, in_6);
  nand nand_3 (nand_3_out, nand_1_out, in_6);
  nand nand_4 (nand_4_out, in_5, nand_2_out);
  nand nand_5 (out_8, nand_3_out, nand_4_out);
  nand nand_6 (nand_6_out, in_1, in_1);
  nand nand_7 (nand_7_out, in_3, in_3);
  // NAND_Gate nand_8 has open pins: in0=nand_6_out, in1=nand_7_out, out=open

  // Notes on the sheet:
  //   Numero 6
  //   Tulio Gomes Braga - 802512
  //   Agora somente usando portas Nand
  //   Or
endmodule

module Numero7 (
  input  in_1,
  input  in_2,
  input  in_3,
  input  in_4,
  output out_5,
  output out_6
);

  wire and_2_out, and_out, nor_1_out, nor_2_out, nor_3_out, not_1_out, not_2_out, xor_out;

  not not_1 (not_1_out, in_1);
  xnor xnor_1 (out_5, not_1_out, not_2_out);
  not not_2 (not_2_out, in_2);
  nor nor_1 (nor_1_out, in_4, in_4);
  nor nor_2 (nor_2_out, in_3, in_3);
  nor \and  (and_out, in_3, nor_1_out);
  nor and_2 (and_2_out, nor_2_out, in_4);
  nor nor_3 (nor_3_out, and_out, and_2_out);
  nor xnor_2 (out_6, xor_out, xor_out);
  nor \xor  (xor_out, nor_3_out, nor_3_out);

  // Notes on the sheet:
  //   Numero 7
  //   Tulio Gomes Braga - 802512 
  //   Agora somente usando portas Nor
endmodule

module Numero8 (
  input  in_1,
  input  in_2,
  input  in_3,
  input  in_4,
  output out_5,
  output out_6
);

  wire and_1_out, nand_1_out, nand_2_out, not_1_out, not_2_out;

  not not_1 (not_1_out, in_1);
  not not_2 (not_2_out, in_2);
  nand nand_1 (nand_1_out, in_3, in_3);
  nand nand_2 (nand_2_out, in_4, in_4);
  not not_3 (out_5, and_1_out);
  and and_1 (and_1_out, not_1_out, not_2_out);
  nand nand_3 (out_6, nand_1_out, nand_2_out);

  // Notes on the sheet:
  //   Numero 8
  //   Tulio Gomes Braga - 802512
  //   Agora somente usando portas Nand
endmodule
