// Logisim project Guia_06.circ as structural Verilog
module Numero1 (
  input  a,
  input  b,
  input  c,
  input  a_2,
  input  b_2,
  input  c_2,
  input  a_3,
  input  b_3,
  input  c_3,
  input  a_4,
  input  b_4,
  input  c_4,
  input  a_5,
  input  b_5,
  input  c_5,
  output out_16,
  output out_17,
  output out_18,
  output out_19,
  output out_20
);

  wire and_1_out, and_2_out, and_3_out, and_4_out, and_5_out, and_6_out, and_7_out, and_8_out, not_1_out,
       not_2_out, not_3_out, not_4_out, not_5_out, not_6_out, not_7_out, not_8_out;

  not not_1 (not_1_out, b);
  not not_2 (not_2_out, b_2);
  not not_3 (not_3_out, c_2);
  not not_4 (not_4_out, c_2);
  not not_5 (not_5_out, a_4);
  not not_6 (not_6_out, c_4);
  not not_7 (not_7_out, b_5);
  and and_1 (and_1_out, not_7_out, not_8_out);
  not not_8 (not_8_out, c_5);
  and and_2 (and_2_out, a_5, b_5);
  and and_3 (and_3_out, not_1_out, c);
  and and_4 (and_4_out, a, c);
  and and_5 (and_5_out, not_2_out, not_3_out);
  and and_6 (and_6_out, a_2, not_4_out);
  or or_1 (out_18, b_3, b_3, b_3);
  and and_7 (and_7_out, not_5_out, c_4);
  and and_8 (and_8_out, b_4, not_6_out);
  or or_2 (out_16, and_3_out, and_4_out);
  or or_3 (out_17, and_5_out, and_6_out);
  or or_4 (out_19, and_7_out, and_8_out);
  or or_5 (out_20, and_1_out, and_2_out);

  // Notes on the sheet:
  //   Numero 1
  //   a)
  //   b)
  //   C)
  //   d)
  //   e)
endmodule

module Numero2 (
  input  a,
  input  b,
  input  c,
  input  a_2,
  input  b_2,
  input  c_2,
  input  a_3,
  input  b_3,
  input  c_3,
  input  a_4,
  input  b_4,
  input  c_4,
  input  a_5,
  input  b_5,
  input  c_5,
  output out_16,
  output out_17,
  output out_18,
  output out_19,
  output out_20
);

  wire not_1_out, not_2_out, not_3_out, not_4_out, not_5_out, not_6_out, not_7_out, not_8_out, not_9_out,
       not_10_out, not_11_out, not_12_out, not_13_out, or_1_out, or_2_out, or_3_out, or_4_out, or_5_out,
       or_6_out, or_7_out, or_9_out, or_10_out, or_11_out;

  not not_1 (not_1_out, a);
  not not_2 (not_2_out, c);
  not not_3 (not_3_out, b);
  not not_4 (not_4_out, c);
  not not_5 (not_5_out, b_2);
  not not_6 (not_6_out, a_2);
  not not_7 (not_7_out, a_3);
  not not_8 (not_8_out, c_3);
  not not_9 (not_9_out, b_3);
  not not_10 (not_10_out, a_5);
  not not_11 (not_11_out, c_5);
  not not_12 (not_12_out, b_5);
  not not_13 (not_13_out, b_5);
  or or_1 (or_1_out, not_1_out, not_2_out);
  or or_2 (or_2_out, not_3_out, not_4_out);
  or or_3 (or_3_out, not_5_out, c_2);
  or or_4 (or_4_out, not_6_out, c_2);
  or or_5 (or_5_out, not_7_out, b_3);
  or or_6 (or_6_out, b_3, not_8_out);
  or or_7 (or_7_out, a_3, not_9_out, c_3);
  or or_8 (out_19, b_4, b_4, b_4);
  or or_9 (or_9_out, not_10_out, b_5, not_11_out);
  or or_10 (or_10_out, a_5, not_12_out);
  or or_11 (or_11_out, not_13_out, c_5);
  and and_1 (out_16, or_1_out, or_2_out);
  and and_2 (out_17, or_3_out, or_4_out);
  and and_3 (out_18, or_5_out, or_6_out, or_7_out);
  and and_4 (out_20, or_9_out, or_10_out, or_11_out);

  // Notes on the sheet:
  //   Numero 2
  //   a)
  //   b)
  //   c)
  //   d)
  //   e)
endmodule

module Numero3 (
  input  A,
  input  B,
  input  C,
  input  D,
  input  A_2,
  input  B_2,
  input  C_2,
  input  D_2,
  input  A_3,
  input  B_3,
  input  C_3,
  input  D_3,
  input  A_4,
  input  B_4,
  input  C_4,
  input  D_4,
  input  A_5,
  input  B_5,
  input  C_5,
  input  D_5,
  output out_21,
  output out_22,
  output out_23,
  output out_24,
  output out_25
);

  wire and_1_out, and_2_out, and_3_out, and_4_out, and_5_out, and_6_out, and_7_out, and_8_out, and_9_out,
       and_10_out, and_11_out, and_12_out, and_13_out, and_14_out, and_15_out, and_16_out, and_17_out,
       and_18_out, and_19_out, and_20_out, not_1_out, not_2_out, not_3_out, not_4_out, not_5_out, not_6_out,
       not_7_out, not_8_out, not_9_out, not_10_out, not_11_out, not_12_out, not_13_out, not_14_out,
       not_15_out, not_16_out, not_17_out, not_18_out, not_19_out, not_20_out, not_21_out, not_22_out,
       not_23_out, not_24_out, not_25_out, not_26_out, not_27_out, not_28_out, not_29_out;

  not not_1 (not_1_out, C_5);
  not not_2 (not_2_out, C_5);
  not not_3 (not_3_out, D_5);
  not not_4 (not_4_out, A_5);
  not not_5 (not_5_out, C_5);
  not not_6 (not_6_out, A_5);
  not not_7 (not_7_out, D_5);
  and and_1 (and_1_out, D, not_8_out);
  not not_8 (not_8_out, C);
  not not_9 (not_9_out, B);
  not not_10 (not_10_out, A);
  not not_11 (not_11_out, B);
  not not_12 (not_12_out, D);
  not not_13 (not_13_out, A_2);
  not not_14 (not_14_out, B_2);
  not not_15 (not_15_out, C_2);
  not not_16 (not_16_out, A_2);
  not not_17 (not_17_out, A_3);
  not not_18 (not_18_out, B_3);
  and and_2 (and_2_out, not_17_out, not_18_out, not_19_out);
  not not_19 (not_19_out, C_3);
  and and_3 (and_3_out, B_3, C_3, D_3);
  and and_4 (and_4_out, A_3, not_20_out, C_3);
  not not_20 (not_20_out, B_3);
  not not_21 (not_21_out, A_3);
  and and_5 (and_5_out, not_21_out, C_3, not_22_out);
  not not_22 (not_22_out, D_3);
  not not_23 (not_23_out, A_4);
  and and_6 (and_6_out, not_23_out, B_4, not_24_out);
  not not_24 (not_24_out, D_4);
  not not_25 (not_25_out, C_4);
  and and_7 (and_7_out, A_4, not_25_out, D_4);
  not not_26 (not_26_out, A_4);
  and and_8 (and_8_out, not_26_out, B_4, C_4);
  not not_27 (not_27_out, A_4);
  and and_9 (and_9_out, not_27_out, C_4, not_28_out);
  not not_28 (not_28_out, D_4);
  and and_10 (and_10_out, B_4, C_4, not_29_out);
  not not_29 (not_29_out, D_4);
  and and_11 (and_11_out, A_5, not_1_out);
  and and_12 (and_12_out, A_5, not_2_out, not_3_out);
  and and_13 (and_13_out, not_4_out, not_5_out, D_5);
  and and_14 (and_14_out, not_6_out, B_5, D_5);
  and and_15 (and_15_out, A_5, B_5, not_7_out);
  and and_16 (and_16_out, A, not_9_out, D);
  and and_17 (and_17_out, not_10_out, not_11_out, C, not_12_out);
  and and_18 (and_18_out, D_2, C_2);
  and and_19 (and_19_out, not_13_out, not_14_out, not_15_out);
  and and_20 (and_20_out, not_16_out, B_2, D_2);
  or or_1 (out_23, and_2_out, and_3_out, and_4_out, and_5_out);
  or or_2 (out_24, and_6_out, and_7_out, and_8_out, and_9_out, and_10_out);
  or or_3 (out_25, and_11_out, and_12_out, and_13_out, and_14_out, and_15_out);
  or or_4 (out_21, and_1_out, and_16_out, and_17_out);
  or or_5 (out_22, and_18_out, and_19_out, and_20_out);

  // Notes on the sheet:
  //   Numero 3
  //   a)
  //   b)
  //   c)
  //   d)
  //   e)
endmodule

module Numero7 (
  input  a,
  input  b,
  input  c,
  output out_4
);

  wire not_1_out, not_2_out, or_1_out, or_2_out;

  not not_1 (not_1_out, b);
  not not_2 (not_2_out, a);
  or or_1 (or_1_out, a, not_1_out);
  or or_2 (or_2_out, not_2_out, b, c);
  and and_1 (out_4, or_1_out, or_2_out);

  // Notes on the sheet:
  //   Numero 7
endmodule

module Numero8 (
  input  A,
  input  B,
  input  C,
  input  D,
  output out_5
);

  wire and_1_out, and_2_out, and_3_out, not_1_out, not_2_out, not_3_out, not_4_out, not_5_out;

  not not_1 (not_1_out, A);
  not not_2 (not_2_out, B);
  not not_3 (not_3_out, A);
  not not_4 (not_4_out, C);
  not not_5 (not_5_out, D);
  and and_1 (and_1_out, A, C);
  and and_2 (and_2_out, not_1_out, not_2_out, C, D);
  and and_3 (and_3_out, not_3_out, B, not_4_out, not_5_out);
  or or_1 (out_5, and_1_out, and_2_out, and_3_out);

  // Notes on the sheet:
  //   Numero 8
endmodule

module Numero4 (
  input  A,
  input  B,
  input  C,
  input  D,
  input  A_2,
  input  B_2,
  input  C_2,
  input  D_2,
  input  A_3,
  input  B_3,
  input  C_3,
  input  D_3,
  input  A_4,
  input  B_4,
  input  C_4,
  input  D_4,
  input  A_5,
  input  B_5,
  input  C_5,
  input  D_5,
  output out_21,
  output out_22,
  output out_23
);

  wire and_1_out, not_1_out, not_2_out, not_3_out, not_4_out, not_5_out, not_6_out, not_7_out, not_8_out,
       not_9_out, not_10_out, not_11_out, not_12_out, not_13_out, not_14_out, not_15_out, not_16_out,
       not_17_out, not_18_out, not_19_out, not_20_out, not_21_out, not_22_out, not_23_out, not_24_out,
       not_25_out, not_26_out, or_1_out, or_2_out, or_3_out, or_4_out, or_5_out, or_6_out, or_10_out,
       or_11_out, or_12_out, or_13_out;

  not not_1 (not_1_out, D);
  not not_2 (not_2_out, B);
  not not_3 (not_3_out, D);
  not not_4 (not_4_out, B);
  not not_5 (not_5_out, B_2);
  not not_6 (not_6_out, B_2);
  not not_7 (not_7_out, C_2);
  not not_8 (not_8_out, A_2);
  not not_9 (not_9_out, B_3);
  not not_10 (not_10_out, A_3);
  not not_11 (not_11_out, A_3);
  not not_12 (not_12_out, B_3);
  not not_13 (not_13_out, D_3);
  not not_14 (not_14_out, D_4);
  not not_15 (not_15_out, A_4);
  not not_16 (not_16_out, B_4);
  not not_17 (not_17_out, D_4);
  not not_18 (not_18_out, B_4);
  not not_19 (not_19_out, C_4);
  not not_20 (not_20_out, D_4);
  not not_21 (not_21_out, A_4);
  not not_22 (not_22_out, B_4);
  not not_23 (not_23_out, C_4);
  not not_24 (not_24_out, B_5);
  not not_25 (not_25_out, C_5);
  not not_26 (not_26_out, D_5);
  or or_1 (or_1_out, B, C, not_1_out);
  or or_2 (or_2_out, A, not_2_out, not_3_out);
  or or_3 (or_3_out, A, B, not_4_out, D);
  or or_4 (or_4_out, A_2, not_5_out, D_2);
  or or_5 (or_5_out, A_2, not_6_out, not_7_out);
  or or_6 (or_6_out, not_8_out, C_2, D_2);
  // OR_Gate or_7 has open pins: in0=A_3, in1=not_9_out, in2=C_3, in3=D_3, out=open
  // OR_Gate or_8 has open pins: in0=not_10_out, in1=B_3, in2=C_3, out=open
  // OR_Gate or_9 has open pins: in0=not_11_out, in1=not_12_out, in2=not_13_out, out=open
  or or_10 (or_10_out, A_4, C_4, not_14_out);
  or or_11 (or_11_out, not_15_out, not_16_out, not_17_out);
  or or_12 (or_12_out, not_18_out, not_19_out, not_20_out);
  or or_13 (or_13_out, not_21_out, not_22_out, not_23_out);
  and and_1 (and_1_out, A_5, B_5, not_25_out, not_26_out);
  // AND_Gate and_2 has open pins: in0=or_1_out, in1=or_2_out, in2=or_3_out, out=open
  and and_3 (out_21, or_4_out, or_5_out, or_6_out);
  and and_4 (out_22, or_10_out, or_11_out, or_12_out, or_13_out);
  or or_14 (out_23, not_24_out, and_1_out);

  // Notes on the sheet:
  //   Numero 4
  //   a) 
  //   b)
  //   c)
  //   d)
  //   e) 
endmodule

module Numero5 (
  input  a,
  input  b,
  input  c,
  output out_4
);

  wire and_1_out, and_2_out, not_1_out, not_2_out;

  not not_1 (not_1_out, b);
  not not_2 (not_2_out, c);
  and and_1 (and_1_out, a, not_1_out);
  and and_2 (and_2_out, a, not_2_out);
  or or_1 (out_4, and_1_out, and_2_out);

  // Notes on the sheet:
  //   Numero5
endmodule

module Numero6 (
  input  A,
  input  B,
  input  C,
  input  D,
  output out_5
);

  wire not_1_out, not_2_out, not_3_out, not_4_out, or_1_out, or_2_out, or_3_out;

  not not_1 (not_1_out, B);
  not not_2 (not_2_out, B);
  not not_3 (not_3_out, C);
  not not_4 (not_4_out, D);
  or or_1 (or_1_out, A, B);
  or or_2 (or_2_out, A, not_1_out);
  or or_3 (or_3_out, not_2_out, not_3_out, not_4_out);
  and and_1 (out_5, or_1_out, or_2_out, or_3_out);

  // Notes on the sheet:
  //   Numero 6
endmodule
