// Logisim project Guia_07.circ as structural Verilog: 7 circuits, main circuit main
module main (
  input  A,
  input  A_2,
  input  B,
  input  B_2,
  input  Chave,
  input  [1:0] in_6,
  input  _00,
  input  _01,
  input  _10,
  input  _11,
  input  [1:0] in_11,
  input  [1:0] in_12,
  input  [2:0] in_13,
  input  in_14,
  input  in_15,
  input  [1:0] in_16,
  input  Seleciono,
  input  in_18,
  input  in_19,
  input  in_20,
  output S1,
  output [1:0] out_22,
  output [1:0] out_23,
  output out_24,
  output [1:0] out_25,
  output [1:0] out_26,
  output [1:0] out_27,
  output [1:0] out_28,
  output out_29,
  output out_30,
  output out_31,
  output out_32
);

  wire and_1_out, and_2_out, button_5_out, button_6_out, multiplexer_5_out, not_1_out;

  Button button_1 ();  // open: out
  Multiplexer #(.enable("false")) multiplexer_1 (.in0(A), .in1(B), .out(S1), .sel(Chave));
  Multiplexer #(.select(2), .enable("false")) multiplexer_2 (
    .in0(_00), .in1(_01), .in2(_10), .in3(_11), .out(out_24), .sel(in_11));
  Button button_2 ();  // open: out
  Button button_3 ();  // open: out
  Multiplexer #(.select(3), .enable("false")) multiplexer_3 (
    .in0(in_14), .in1(in_15), .in2(in_15), .in3(in_14), .in4(in_15), .in5(in_14), .in6(in_14), .in7(in_15),
    .out(out_29), .sel(in_13));
  Multiplexer #(.select(3), .enable("false")) multiplexer_4 (
    .in0(in_14), .in1(in_14), .in2(in_14), .in3(in_15), .in4(in_14), .in5(in_15), .in6(in_15), .in7(in_15),
    .out(out_30), .sel(in_13));
  Button button_4 ();  // open: out
  Button button_5 (.out(button_5_out));
  and and_1 (and_1_out, A_2, not_1_out);
  not not_1 (not_1_out, button_5_out);
  and and_2 (and_2_out, B_2, button_5_out);
  // RGBLed rgbled_1: pin names not known; wires that end beside it: and_2_out, and_1_out
  // Buzzer buzzer_1: pin names not known; wires that end beside it: and_2_out
  Multiplexer #(.enable("false")) multiplexer_5 (.in0(Seleciono), .in1(in_18), .out(multiplexer_5_out), .sel(in_19));
  Demultiplexer #(.enable("false")) demultiplexer_1 (.out0(out_31), .out1(out_32), .in(multiplexer_5_out), .sel(in_20));
  Demultiplexer #(.width(2), .enable("false")) demultiplexer_2 (
    .out0(out_22), .out1(out_23), .in(in_6), .sel(button_6_out));
  Button button_6 (.out(button_6_out));
  Demultiplexer #(.select(2), .width(2), .enable("false")) demultiplexer_3 (
    .out0(out_25), .out1(out_26), .out2(out_27), .out3(out_28), .in(in_12), .sel(in_16));

  // Notes on the sheet:
  //   Se a chave estiver aberta o B manda
  //   Implementacao video 2
  //   O numero que tiver ai dentro sera a porta que manda
  //   Boiadeiro colocando o gado nos currais, selecionando portas.
  //   Vem aqui por favor voce, agora vai ali pra mim
  //   Direciono
  //   Se apertar o botao a saida vai pra s2
endmodule

module Numero1 (
  input  A,
  input  A_2,
  input  B,
  input  B_2,
  input  in_5,
  input  in_6,
  output out_7,
  output out_8,
  output out_9
);

  wire nand_1_out, nand_2_out, nand_3_out, nand_4_out;

  nand nand_1 (nand_1_out, in_5, in_5);
  and and_1 (out_7, A, nand_1_out);
  and and_2 (out_9, B, in_5);
  nand nand_2 (nand_2_out, in_6, in_6);
  nand nand_3 (nand_3_out, A_2, nand_2_out);
  nand nand_4 (nand_4_out, B_2, in_6);
  nand nand_5 (out_8, nand_3_out, nand_4_out);

  // Notes on the sheet:
  //   Numero 1
endmodule

module Numero2 (
  input  A,
  input  B,
  input  in_3,
  output out_4
);

  wire nor_1_out, nor_2_out, nor_3_out, nor_4_out, nor_5_out, or_1_out, or_2_out;

  nor nor_1 (nor_1_out, A, A);
  or or_1 (or_1_out, nor_1_out, in_3);
  nor nor_2 (nor_2_out, B, B);
  nor nor_3 (nor_3_out, in_3, in_3);
  or or_2 (or_2_out, nor_2_out, nor_3_out);
  nor nor_4 (nor_4_out, or_1_out, or_1_out);
  nor nor_5 (nor_5_out, or_2_out, or_2_out);
  or or_3 (out_4, nor_4_out, nor_5_out);

  // Notes on the sheet:
  //   Numero 2
endmodule

module Numero3 (
  input  A,
  input  B,
  input  in_3,
  input  A_2,
  input  in_5,
  input  B_2,
  input  in_7,
  output out_8
);

  wire nand_1_out, nand_2_out, nand_3_out, nand_4_out, nand_5_out, nand_6_out, nand_7_out, nor_1_out,
       nor_2_out, nor_3_out, nor_4_out, nor_5_out, or_1_out, or_2_out, or_3_out;

  nor nor_1 (nor_1_out, A, A);
  or or_1 (or_1_out, nor_1_out, in_3);
  nor nor_2 (nor_2_out, B, B);
  nor nor_3 (nor_3_out, in_3, in_3);
  nand nand_1 (nand_1_out, A_2, nand_2_out);
  nand nand_2 (nand_2_out, in_7, in_7);
  nand nand_3 (nand_3_out, B_2, in_7);
  or or_2 (or_2_out, nor_2_out, nor_3_out);
  nor nor_4 (nor_4_out, or_1_out, or_1_out);
  nor nor_5 (nor_5_out, or_2_out, or_2_out);
  nand nand_4 (nand_4_out, nand_1_out, nand_3_out);
  or or_3 (or_3_out, nor_4_out, nor_5_out);
  nand nand_5 (nand_5_out, in_5, in_5);
  nand nand_6 (nand_6_out, or_3_out, nand_5_out);
  nand nand_7 (nand_7_out, nand_4_out, in_5);
  nand nand_8 (out_8, nand_6_out, nand_7_out);

  // Notes on the sheet:
  //   Numero 3
endmodule

module Numero4 (
  input  in_1,
  input  in_2,
  input  in_3,
  output out_4
);

  wire xnor_1_out, xor_1_out;

  xor xor_1 (xor_1_out, in_1, in_2);
  xnor xnor_1 (xnor_1_out, in_1, in_2);
  Multiplexer #(.enable("false")) multiplexer_1 (.in0(xor_1_out), .in1(xnor_1_out), .out(out_4), .sel(in_3));

  // Notes on the sheet:
  //   Numero 4
  //   Mux >> a.e + b.e'
  //   Professor nao consegui adaptar a expressao para que possa forma o mux em si como nas questoes anteriores
  //   Expressao: (a.b + a'.b')'
endmodule

module Numero5 (
  input  in_1,
  input  in_2,
  input  [2:0] in_3,
  output out_4
);

  wire and_1_out, nand_1_out, nor_1_out, not_1_out, not_2_out, or_1_out, xnor_1_out, xor_1_out;

  and and_1 (and_1_out, in_1, in_2);
  or or_1 (or_1_out, in_1, in_2);
  nand nand_1 (nand_1_out, in_1, in_2);
  nor nor_1 (nor_1_out, in_1, in_2);
  xor xor_1 (xor_1_out, in_1, in_2);
  xnor xnor_1 (xnor_1_out, in_1, in_2);
  not not_1 (not_1_out, in_1);
  not not_2 (not_2_out, in_2);
  Multiplexer #(.select(3), .enable("false")) multiplexer_1 (
    .in0(not_1_out), .in1(not_2_out), .in2(and_1_out), .in3(or_1_out), .in4(nand_1_out), .in5(nor_1_out),
    .in6(xor_1_out), .in7(xnor_1_out), .out(out_4), .sel(in_3));

  // Notes on the sheet:
  //   Numero 5
endmodule

module Numero6 (
  input  [1:0] in_1,
  input  [1:0] in_2,
  output [1:0] out_3
);

  wire [1:0] xor_1_out;

  assign xor_1_out = in_1 ^ in_2;  // XOR_Gate xor_1, 2 bits wide
  assign out_3 = ~xor_1_out;  // XNOR_Gate xnor_1, 2 bits wide XNOR_Gate

  // Notes on the sheet:
  //   Numero 6
  //   Onde eles são iguais a posicao da saida sera 1, aonde sao diferentes a saida sera 0
endmodule
