// Logisim project Guia_08.circ as structural Verilog: 13 circuits, main circuit main
module main (
);


  // Notes on the sheet:
  //   Tulio Gomes Braga
  //   802512
endmodule

module Meio_Somador (
  input  A,
  input  B,
  output V,
  output S
);

  wire and_1_out, and_2_out, not_1_out, not_2_out;

  not not_1 (not_1_out, A);
  not not_2 (not_2_out, B);
  and and_1 (and_1_out, not_1_out, B);
  and and_2 (and_2_out, A, not_2_out);
  and and_3 (V, A, B);
  or or_1 (S, and_1_out, and_2_out);

  // Notes on the sheet:
  //   Somador de 2bits
endmodule

module Somador_Completo (
  input  A,
  input  B,
  input  Vem,
  output S,
  output Vai
);

  wire and_1_out, and_2_out, and_3_out, and_4_out, and_5_out, and_6_out, and_7_out, and_8_out, not_1_out,
       not_2_out, not_3_out;

  not not_1 (not_1_out, A);
  not not_2 (not_2_out, B);
  not not_3 (not_3_out, Vem);
  and and_1 (and_1_out, not_1_out, not_2_out, Vem);
  and and_2 (and_2_out, not_1_out, B, not_3_out);
  and and_3 (and_3_out, A, not_2_out, not_3_out);
  and and_4 (and_4_out, A, B, Vem);
  and and_5 (and_5_out, not_1_out, B, Vem);
  and and_6 (and_6_out, A, not_2_out, Vem);
  and and_7 (and_7_out, A, B, not_3_out);
  and and_8 (and_8_out, A, B, Vem);
  or or_1 (S, and_1_out, and_2_out, and_3_out, and_4_out);
  or or_2 (Vai, and_5_out, and_6_out, and_7_out, and_8_out);

  // Notes on the sheet:
  //   Somador de 3bits
endmodule

module Subtrator (
  input  A,
  input  B,
  output S,
  output Borrow
);

  wire and_1_out, and_2_out, not_1_out, not_2_out;

  not not_1 (not_1_out, A);
  not not_2 (not_2_out, B);
  and and_1 (and_1_out, not_1_out, B);
  and and_2 (and_2_out, A, not_2_out);
  and and_3 (Borrow, not_1_out, B);
  or or_1 (S, and_1_out, and_2_out);

  // Notes on the sheet:
  //   Subtrator de 2bits
endmodule

module Subtrator_Completo (
  input  A,
  input  B,
  input  Bin,
  output S,
  output Bout
);

  wire and_1_out, and_2_out, and_3_out, not_1_out, not_2_out, not_3_out, xor_1_out;

  not not_1 (not_1_out, A);
  not not_2 (not_2_out, Bin);
  not not_3 (not_3_out, B);
  xor xor_1 (xor_1_out, A, B);
  and and_1 (and_1_out, not_1_out, Bin);
  and and_2 (and_2_out, not_1_out, B);
  and and_3 (and_3_out, B, Bin);
  xor xor_2 (S, xor_1_out, Bin);
  or or_1 (Bout, and_1_out, and_2_out, and_3_out);

  // Notes on the sheet:
  //   Subtrator de 3bits
endmodule

module Numero1 (
  input  in_1,
  input  in_2,
  input  in_3,
  input  in_4,
  input  in_5,
  input  in_6,
  input  in_7,
  input  in_8,
  input  in_9,
  input  in_10,
  output S5,
  output S4,
  output S3,
  output S2,
  output S1,
  output S0
);

  wire somador_completo_2_vai, somador_completo_3_vai, somador_completo_4_vai, somador_completo_5_vai;

  Somador_Completo somador_completo_1 (.A(in_1), .B(in_6), .Vem(somador_completo_2_vai), .S(S4), .Vai(S5));
  Somador_Completo somador_completo_2 (
    .A(in_2), .B(in_7), .Vem(somador_completo_3_vai), .S(S3), .Vai(somador_completo_2_vai));
  Somador_Completo somador_completo_3 (
    .A(in_3), .B(in_8), .Vem(somador_completo_4_vai), .S(S2), .Vai(somador_completo_3_vai));
  Somador_Completo somador_completo_4 (
    .A(in_4), .B(in_9), .Vem(somador_completo_5_vai), .S(S1), .Vai(somador_completo_4_vai));
  Somador_Completo somador_completo_5 (.A(in_5), .B(in_10), .Vem(1'b0), .S(S0), .Vai(somador_completo_5_vai));

  // Notes on the sheet:
  //   Numero 1
endmodule

module Numero_2 (
  input  in_1,
  input  in_2,
  input  in_3,
  input  in_4,
  input  in_5,
  input  in_6,
  input  in_7,
  input  in_8,
  input  in_9,
  input  in_10,
  input  in_11,
  input  in_12,
  output out_13,
  output out_14,
  output out_15,
  output out_16,
  output out_17,
  output out_18,
  output out_19
);

  wire subtrator_completo_2_bout, subtrator_completo_3_bout, subtrator_completo_4_bout,
       subtrator_completo_5_bout, subtrator_completo_6_bout;

  Subtrator_Completo subtrator_completo_1 (
    .A(in_1), .B(in_7), .Bin(subtrator_completo_2_bout), .S(out_14), .Bout(out_13));
  Subtrator_Completo subtrator_completo_2 (
    .A(in_2), .B(in_8), .Bin(subtrator_completo_3_bout), .S(out_15), .Bout(subtrator_completo_2_bout));
  Subtrator_Completo subtrator_completo_3 (
    .A(in_3), .B(in_9), .Bin(subtrator_completo_4_bout), .S(out_16), .Bout(subtrator_completo_3_bout));
  Subtrator_Completo subtrator_completo_4 (
    .A(in_4), .B(in_10), .Bin(subtrator_completo_5_bout), .S(out_17), .Bout(subtrator_completo_4_bout));
  Subtrator_Completo subtrator_completo_5 (
    .A(in_5), .B(in_11), .Bin(subtrator_completo_6_bout), .S(out_18), .Bout(subtrator_completo_5_bout));
  Subtrator_Completo subtrator_completo_6 (
    .A(in_6), .B(in_12), .Bin(1'b0), .S(out_19), .Bout(subtrator_completo_6_bout));

  // Notes on the sheet:
  //   Numero 2
endmodule

module Comparador (
  input  A,
  input  B,
  output A_B,
  output A__B,
  output A_B_2
);

  wire not_1_out, not_2_out;

  not not_1 (not_1_out, A);
  not not_2 (not_2_out, B);
  and and_1 (A_B, A, not_2_out);
  xnor xnor_1 (A__B, A, B);
  and and_2 (A_B_2, not_1_out, B);
endmodule

module Numero_3 (
  input  in_1,
  input  in_2,
  input  in_3,
  input  in_4,
  input  in_5,
  input  in_6,
  input  in_7,
  input  in_8,
  input  in_9,
  input  in_10,
  input  in_11,
  input  in_12
);

  wire comparador_1_a__b, comparador_1_a_b, comparador_1_a_b_2, comparador_2_a__b, comparador_2_a_b,
       comparador_2_a_b_2, comparador_3_a__b, comparador_3_a_b, comparador_3_a_b_2, comparador_4_a__b,
       comparador_4_a_b, comparador_4_a_b_2, comparador_5_a__b, comparador_5_a_b, comparador_5_a_b_2,
       comparador_6_a__b, comparador_6_a_b, comparador_6_a_b_2;

  Comparador comparador_1 (
    .A(in_1), .B(in_7), .A_B(comparador_1_a_b), .A__B(comparador_1_a__b), .A_B_2(comparador_1_a_b_2));
  LED led_1 (.in(comparador_1_a__b));
  LED led_2 (.in(comparador_1_a_b));
  LED led_3 (.in(comparador_1_a_b_2));
  Comparador comparador_2 (
    .A(in_2), .B(in_8), .A_B(comparador_2_a_b), .A__B(comparador_2_a__b), .A_B_2(comparador_2_a_b_2));
  LED led_4 (.in(comparador_2_a__b));
  LED led_5 (.in(comparador_2_a_b));
  LED led_6 (.in(comparador_2_a_b_2));
  Comparador comparador_3 (
    .A(in_3), .B(in_9), .A_B(comparador_3_a_b), .A__B(comparador_3_a__b), .A_B_2(comparador_3_a_b_2));
  LED led_7 (.in(comparador_4_a_b_2));
  LED led_8 (.in(comparador_3_a__b));
  LED led_9 (.in(comparador_3_a_b_2));
  LED led_10 (.in(comparador_3_a_b));
  Comparador comparador_4 (
    .A(in_4), .B(in_10), .A_B(comparador_4_a_b), .A__B(comparador_4_a__b), .A_B_2(comparador_4_a_b_2));
  LED led_11 (.in(comparador_4_a__b));
  LED led_12 (.in(comparador_5_a_b_2));
  LED led_13 (.in(comparador_4_a_b));
  Comparador comparador_5 (
    .A(in_5), .B(in_11), .A_B(comparador_5_a_b), .A__B(comparador_5_a__b), .A_B_2(comparador_5_a_b_2));
  LED led_14 (.in(comparador_5_a_b));
  LED led_15 (.in(comparador_6_a__b));
  LED led_16 (.in(comparador_6_a_b_2));
  LED led_17 (.in(comparador_5_a__b));
  Comparador comparador_6 (
    .A(in_6), .B(in_12), .A_B(comparador_6_a_b), .A__B(comparador_6_a__b), .A_B_2(comparador_6_a_b_2));
  LED led_18 (.in(comparador_6_a_b));

  // Notes on the sheet:
  //   Numero 3
  //   Legenda:
  //   Vermelho: A<B
  //   Amarelo: A==B
  //   Verde: A>B
  //   A
  //   S5
  //   S4
  //   S3
  //   B
  //   S2
  //   S0
  //   S1
endmodule

module Comparador_Desigualdade (
  input  A,
  input  B,
  output A__B,
  output A__B_2
);

  wire not_1_out, not_2_out;

  not not_1 (not_1_out, A);
  not not_2 (not_2_out, B);
  xor xor_1 (A__B, A, B);
  xnor xnor_1 (A__B_2, A, B);
endmodule

module Numero_4 (
  input  in_1,
  input  in_2,
  input  in_3,
  input  in_4,
  input  in_5,
  input  in_6,
  input  in_7,
  input  in_8,
  input  in_9,
  input  in_10,
  input  in_11,
  input  in_12
);

  wire comparador_desigualdade_1_a__b, comparador_desigualdade_1_a__b_2, comparador_desigualdade_2_a__b,
       comparador_desigualdade_2_a__b_2, comparador_desigualdade_3_a__b, comparador_desigualdade_3_a__b_2,
       comparador_desigualdade_4_a__b, comparador_desigualdade_4_a__b_2, comparador_desigualdade_5_a__b,
       comparador_desigualdade_5_a__b_2, comparador_desigualdade_6_a__b, comparador_desigualdade_6_a__b_2;

  Comparador_Desigualdade comparador_desigualdade_1 (
    .A(in_1), .B(in_7), .A__B(comparador_desigualdade_1_a__b), .A__B_2(comparador_desigualdade_1_a__b_2));
  LED led_1 (.in(comparador_desigualdade_1_a__b_2));
  LED led_2 (.in(comparador_desigualdade_1_a__b));
  Comparador_Desigualdade comparador_desigualdade_2 (
    .A(in_2), .B(in_8), .A__B(comparador_desigualdade_2_a__b), .A__B_2(comparador_desigualdade_2_a__b_2));
  LED led_3 (.in(comparador_desigualdade_2_a__b_2));
  LED led_4 (.in(comparador_desigualdade_2_a__b));
  Comparador_Desigualdade comparador_desigualdade_3 (
    .A(in_3), .B(in_9), .A__B(comparador_desigualdade_3_a__b), .A__B_2(comparador_desigualdade_3_a__b_2));
  LED led_5 (.in(comparador_desigualdade_3_a__b_2));
  LED led_6 (.in(comparador_desigualdade_3_a__b));
  Comparador_Desigualdade comparador_desigualdade_4 (
    .A(in_4), .B(in_10), .A__B(comparador_desigualdade_4_a__b), .A__B_2(comparador_desigualdade_4_a__b_2));
  LED led_7 (.in(comparador_desigualdade_5_a__b_2));
  LED led_8 (.in(comparador_desigualdade_4_a__b));
  LED led_9 (.in(comparador_desigualdade_4_a__b_2));
  Comparador_Desigualdade comparador_desigualdade_5 (
    .A(in_5), .B(in_11), .A__B(comparador_desigualdade_5_a__b), .A__B_2(comparador_desigualdade_5_a__b_2));
  LED led_10 (.in(comparador_desigualdade_6_a__b_2));
  LED led_11 (.in(comparador_desigualdade_5_a__b));
  Comparador_Desigualdade comparador_desigualdade_6 (
    .A(in_6), .B(in_12), .A__B(comparador_desigualdade_6_a__b), .A__B_2(comparador_desigualdade_6_a__b_2));
  LED led_12 (.in(comparador_desigualdade_6_a__b));

  // Notes on the sheet:
  //   Numero 4
  //   Legenda:
  //   Vermelho: A==B
  //   Verde: A!=B
  //   A
  //   S5
  //   S4
  //   S3
  //   B
  //   S2
  //   S0
  //   S1
endmodule

module Numero_5 (
  input  in_1,
  input  in_2,
  input  in_3,
  input  in_4,
  input  in_5,
  output out_6,
  output out_7,
  output out_8,
  output out_9,
  output out_10,
  output out_11
);

  wire not_1_out, not_2_out, not_3_out, not_4_out, not_5_out;

  not not_1 (not_1_out, in_1);
  not not_2 (not_2_out, in_3);
  not not_3 (not_3_out, in_2);
  not not_4 (not_4_out, in_4);
  not not_5 (not_5_out, in_5);
  Numero1 numero1_1 (
    .in_1(not_1_out), .in_2(not_3_out), .in_3(not_2_out), .in_4(not_4_out), .in_5(not_5_out), .in_6(1'b0),
    .in_7(1'b0), .in_8(1'b0), .in_9(1'b0), .in_10(1'b1), .S5(out_6), .S4(out_7), .S3(out_8), .S2(out_9),
    .S1(out_10), .S0(out_11));

  // Notes on the sheet:
  //   Numero 5
endmodule

module Numero_7 (
  input  in_1,
  input  in_2,
  input  A,
  input  in_4,
  input  in_5,
  input  in_6,
  input  in_7,
  input  B,
  input  in_9,
  input  in_10,
  input  in_11
);

  wire comparador_desigualdade_1_a__b, comparador_desigualdade_1_a__b_2, comparador_desigualdade_2_a__b,
       comparador_desigualdade_2_a__b_2, comparador_desigualdade_3_a__b, comparador_desigualdade_3_a__b_2,
       comparador_desigualdade_4_a__b, comparador_desigualdade_4_a__b_2, comparador_desigualdade_5_a__b,
       comparador_desigualdade_5_a__b_2, multiplexer_1_out, multiplexer_2_out, multiplexer_3_out,
       multiplexer_4_out, multiplexer_5_out;

  Comparador_Desigualdade comparador_desigualdade_1 (
    .A(in_1), .B(in_6), .A__B(comparador_desigualdade_1_a__b), .A__B_2(comparador_desigualdade_1_a__b_2));
  Comparador_Desigualdade comparador_desigualdade_2 (
    .A(in_2), .B(in_7), .A__B(comparador_desigualdade_2_a__b), .A__B_2(comparador_desigualdade_2_a__b_2));
  Multiplexer #(.enable("false")) multiplexer_1 (
    .in0(comparador_desigualdade_2_a__b_2), .in1(comparador_desigualdade_2_a__b), .out(multiplexer_1_out),
    .sel(in_11));
  Multiplexer #(.enable("false")) multiplexer_2 (
    .in0(comparador_desigualdade_1_a__b_2), .in1(comparador_desigualdade_1_a__b), .out(multiplexer_2_out),
    .sel(in_11));
  LED led_1 (.in(multiplexer_1_out));
  LED led_2 (.in(multiplexer_2_out));
  Comparador_Desigualdade comparador_desigualdade_3 (
    .A(A), .B(B), .A__B(comparador_desigualdade_3_a__b), .A__B_2(comparador_desigualdade_3_a__b_2));
  Multiplexer #(.enable("false")) multiplexer_3 (
    .in0(comparador_desigualdade_3_a__b_2), .in1(comparador_desigualdade_3_a__b), .out(multiplexer_3_out),
    .sel(in_11));
  LED led_3 (.in(multiplexer_3_out));
  Comparador_Desigualdade comparador_desigualdade_4 (
    .A(in_5), .B(in_10), .A__B(comparador_desigualdade_4_a__b), .A__B_2(comparador_desigualdade_4_a__b_2));
  Comparador_Desigualdade comparador_desigualdade_5 (
    .A(in_4), .B(in_9), .A__B(comparador_desigualdade_5_a__b), .A__B_2(comparador_desigualdade_5_a__b_2));
  Multiplexer #(.enable("false")) multiplexer_4 (
    .in0(comparador_desigualdade_5_a__b_2), .in1(comparador_desigualdade_5_a__b), .out(multiplexer_4_out),
    .sel(in_11));
  LED led_4 (.in(multiplexer_4_out));
  Multiplexer #(.enable("false")) multiplexer_5 (
    .in0(comparador_desigualdade_4_a__b_2), .in1(comparador_desigualdade_4_a__b), .out(multiplexer_5_out),
    .sel(in_11));
  LED led_5 (.in(multiplexer_5_out));

  // Notes on the sheet:
  //   Numero 7
  //   Legenda:
  //   0 igualdade
  //   1 desigualdade
  //   Verde: Legenda Verdadeira
  //   Vermelho:    Legenda Falsa
endmodule
