// Logisim project R01_0103.circ as structural Verilog
module a (
  input  a,
  input  b,
  input  c,
  input  d,
  output out_5
);

  wire nand_1_out, nand_2_out;

  nand nand_1 (nand_1_out, a, c);
  nand nand_2 (nand_2_out, b, d);
  nand nand_3 (out_5, nand_1_out, nand_2_out);
endmodule

module b (
  input  a,
  input  b,
  input  c,
  output out_4
);

  wire multiplexer_1_out, multiplexer_2_out, not_1_out, not_2_out, not_3_out;

  Multiplexer #(.enable("false")) multiplexer_1 (.in0(b), .in1(c), .out(multiplexer_1_out), .sel(a));
  not not_1 (not_1_out, a);
  Multiplexer #(.enable("false")) multiplexer_2 (.in0(not_1_out), .in1(not_2_out), .out(multiplexer_2_out), .sel(c));
  not not_2 (not_2_out, b);
  not not_3 (not_3_out, c);
  Multiplexer #(.enable("false")) multiplexer_3 (
    .in0(multiplexer_1_out), .in1(multiplexer_2_out), .out(out_4), .sel(not_3_out));
endmodule
