// Logisim project R01_0101.circ as structural Verilog: 7 circuits, main circuit main
module main (
);


  // Notes on the sheet:
  //   Tulio Gomes Braga - 802512
endmodule

module a (
  input  a,
  input  b,
  input  c,
  input  d,
  output out_5
);

  wire and_1_out, and_2_out, and_3_out, and_4_out, and_5_out, and_6_out, and_7_out, not_1_out, not_2_out,
       not_3_out, not_4_out;

  not not_1 (not_1_out, a);
  not not_2 (not_2_out, b);
  not not_3 (not_3_out, c);
  not not_4 (not_4_out, d);
  and and_1 (and_1_out, not_1_out, not_2_out, not_3_out, not_4_out);
  and and_2 (and_2_out, not_1_out, not_2_out, not_3_out, d);
  and and_3 (and_3_out, not_1_out, not_2_out, c, not_4_out);
  and and_4 (and_4_out, not_1_out, not_2_out, c, d);
  and and_5 (and_5_out, not_1_out, b, not_3_out, d);
  and and_6 (and_6_out, a, not_2_out, not_3_out, not_4_out);
  and and_7 (and_7_out, a, b, not_3_out, d);
  or or_1 (out_5, and_1_out, and_2_out, and_3_out, and_4_out, and_5_out, and_6_out, and_7_out);
endmodule

module b (
  input  A,
  input  B,
  input  C,
  input  D,
  output out_5
);

  wire not_1_out, not_2_out, not_3_out, not_4_out, or_1_out, or_2_out, or_3_out, or_4_out, or_5_out,
       or_6_out, or_7_out, or_8_out, or_9_out;

  not not_1 (not_1_out, A);
  not not_2 (not_2_out, C);
  not not_3 (not_3_out, B);
  not not_4 (not_4_out, D);
  or or_1 (or_1_out, A, not_3_out, C, D);
  or or_2 (or_2_out, A, not_3_out, not_2_out, D);
  or or_3 (or_3_out, A, not_3_out, not_2_out, not_4_out);
  or or_4 (or_4_out, not_1_out, B, C, not_4_out);
  or or_5 (or_5_out, not_1_out, B, not_2_out, D);
  or or_6 (or_6_out, not_1_out, B, not_2_out, not_4_out);
  or or_7 (or_7_out, not_1_out, not_3_out, C, D);
  or or_8 (or_8_out, not_1_out, not_3_out, not_2_out, D);
  or or_9 (or_9_out, not_1_out, not_3_out, not_2_out, not_4_out);
  and and_1 (out_5, or_1_out, or_2_out, or_3_out, or_4_out, or_5_out, or_6_out, or_7_out, or_8_out, or_9_out);
endmodule

module c (
  input  a_A,
  input  b_B,
  input  c_C,
  input  d_D,
  output out_5
);

  wire and_1_out, and_2_out, and_3_out, not_1_out, not_2_out, not_3_out, not_4_out;

  not not_1 (not_1_out, b_B);
  not not_2 (not_2_out, a_A);
  not not_3 (not_3_out, d_D);
  not not_4 (not_4_out, c_C);
  and and_1 (and_1_out, not_2_out, not_1_out);
  and and_2 (and_2_out, b_B, not_4_out, d_D);
  and and_3 (and_3_out, not_1_out, not_4_out, not_3_out);
  or or_1 (out_5, and_1_out, and_2_out, and_3_out);
endmodule

module d (
  input  a_A,
  input  b_B,
  input  c_C,
  input  d_D,
  output out_5
);

  wire not_1_out, not_2_out, not_3_out, not_4_out, or_1_out, or_2_out, or_3_out, or_4_out;

  not not_1 (not_1_out, b_B);
  not not_2 (not_2_out, a_A);
  not not_3 (not_3_out, c_C);
  not not_4 (not_4_out, d_D);
  or or_1 (or_1_out, not_1_out, not_3_out);
  or or_2 (or_2_out, not_2_out, b_B, not_3_out);
  or or_3 (or_3_out, not_2_out, b_B, not_4_out);
  or or_4 (or_4_out, not_1_out, c_C, d_D);
  and and_1 (out_5, or_1_out, or_2_out, or_3_out, or_4_out);
endmodule

module e (
  input  a,
  input  b,
  input  c,
  input  d,
  output out_5
);

  wire nand_1_out, nand_2_out, nand_3_out, nand_4_out, nand_5_out, nand_6_out, nand_7_out, nand_8_out,
       nand_9_out, not_1_out, not_2_out, not_3_out, not_4_out;

  not not_1 (not_1_out, b);
  not not_2 (not_2_out, a);
  not not_3 (not_3_out, d);
  not not_4 (not_4_out, c);
  nand nand_1 (nand_1_out, not_2_out, not_1_out);
  nand nand_2 (nand_2_out, b, not_4_out, d);
  nand nand_3 (nand_3_out, not_1_out, not_4_out, not_3_out);
  nand nand_4 (nand_4_out, nand_1_out, nand_1_out);
  nand nand_5 (nand_5_out, nand_2_out, nand_2_out);
  nand nand_6 (nand_6_out, nand_3_out, nand_3_out);
  nand nand_7 (nand_7_out, nand_4_out, nand_4_out);
  nand nand_8 (nand_8_out, nand_5_out, nand_5_out);
  nand nand_9 (nand_9_out, nand_6_out, nand_6_out);
  nand nand_10 (out_5, nand_7_out, nand_8_out, nand_9_out);
endmodule

module f (
  input  a,
  input  b,
  input  c,
  input  d,
  output out_5
);

  wire nor_1_out, nor_2_out, nor_3_out, nor_4_out, nor_5_out, nor_6_out, nor_7_out, nor_8_out, nor_9_out,
       nor_10_out, nor_11_out, nor_12_out, not_1_out, not_2_out, not_3_out, not_4_out;

  not not_1 (not_1_out, a);
  not not_2 (not_2_out, b);
  not not_3 (not_3_out, d);
  not not_4 (not_4_out, c);
  nor nor_1 (nor_1_out, not_2_out, not_4_out);
  nor nor_2 (nor_2_out, not_1_out, b, not_4_out);
  nor nor_3 (nor_3_out, not_1_out, b, not_3_out);
  nor nor_4 (nor_4_out, not_2_out, c, d);
  nor nor_5 (nor_5_out, nor_1_out, nor_1_out);
  nor nor_6 (nor_6_out, nor_2_out, nor_2_out);
  nor nor_7 (nor_7_out, nor_3_out, nor_3_out);
  nor nor_8 (nor_8_out, nor_4_out, nor_4_out);
  nor nor_9 (nor_9_out, nor_5_out, nor_5_out);
  nor nor_10 (nor_10_out, nor_6_out, nor_6_out);
  nor nor_11 (nor_11_out, nor_7_out, nor_7_out);
  nor nor_12 (nor_12_out, nor_8_out, nor_8_out);
  nor nor_13 (out_5, nor_9_out, nor_10_out, nor_11_out, nor_12_out);
endmodule
